// Logisim project LilHexCrusher.circ as structural Verilog: 6 circuits, main circuit main
module main (
  input  RESET
);

  wire _1_out, _2_out, _3_out, _4_out, CLK, EnableReadMem, EnableReadReg, EnableWRTMem, LAC_out,
       multiplexer_1_out, multiplexer_2_out, multiplexer_4_out, pcenable;
  wire [3:0] acin, acout, MemAddr, RegAddr1, RegAddr2, WrtAddrreg;
  wire [7:0] ReadMem, RegData1, RegData2, WrtRegData;
  wire [11:4] controlled_buffer_2_out, controlled_buffer_8_out;
  wire [11:8] controlled_buffer_7_out;
  wire [13:0] controlled_buffer_1_out, Rest;
  wire [15:0] adder_3_out, adder_7_out, MemWrtData, multiplexer_3_out, pcin, pcout;
  wire [15:14] instruction_memory_1_instruction;

  Instruction_memory instruction_memory_1 (
    .Read_address(pcout),
    .Instruction({instruction_memory_1_instruction, Rest[13:10], RegAddr2, RegAddr1, Rest[1:0]}));
  and jmp (pcenable, ~instruction_memory_1_instruction[14], instruction_memory_1_instruction[15]);  // AND_Gate
  and LAC (LAC_out, instruction_memory_1_instruction[14], instruction_memory_1_instruction[15]);
  assign controlled_buffer_1_out = pcenable ? {Rest[13:10], RegAddr2, RegAddr1, Rest[1:0]} : 14'bz;  // Controlled_Buffer controlled_buffer_1
  assign pcin = {{2{1'b0}}, controlled_buffer_1_out};  // Bit_Extender bit_extender_1
  and add (EnableReadReg, ~instruction_memory_1_instruction[14], ~instruction_memory_1_instruction[15]);  // AND_Gate
  and _1 (_1_out, Rest[0], Rest[1]);
  and _2 (_2_out, Rest[0], Rest[1]);
  assign {controlled_buffer_2_out, RegAddr1} = _2_out ? {Rest[13:10], RegAddr2, RegAddr1} : 12'bz;  // Controlled_Buffer controlled_buffer_2
  assign MemAddr = LAC_out ? acout : 4'bz;  // Controlled_Buffer controlled_buffer_3
  Mem16 mem16_1 (
    .Address(MemAddr), .Write_Data(MemWrtData), .Read_Data(ReadMem), .Write(multiplexer_1_out), .clk(CLK),
    .reset(RESET), .Read(multiplexer_2_out));
  Clock u_CLK (.out(CLK));
  Multiplexer #(.enable("false")) multiplexer_1 (.in0(1'b0), .in1(1'b1), .out(multiplexer_1_out), .sel(EnableWRTMem));
  Multiplexer #(.enable("false")) multiplexer_2 (.in0(1'b0), .in1(1'b1), .out(multiplexer_2_out), .sel(EnableReadMem));
  assign WrtAddrreg = _1_out ? RegAddr1 : 4'bz;  // Controlled_Buffer controlled_buffer_4
  Adder adder_1 (.a(RegData1), .b(RegData2), .out(WrtRegData));  // open: cin, cout
  assign WrtAddrreg = _2_out ? RegAddr1 : 4'bz;  // Controlled_Buffer controlled_buffer_5
  Adder adder_2 (.a(RegData1), .b(controlled_buffer_2_out), .out(WrtRegData));  // open: cin, cout
  assign WrtAddrreg = LAC_out ? {RegAddr1[1:0], Rest[1:0]} : 4'bz;  // Controlled_Buffer controlled_buffer_6
  Counter #(.width(4), .max('hf)) ACum (.D(acin), .Q(acout), .clk(CLK), .clr(RESET));  // open: load, count, carry
  and _3 (_3_out, Rest[0], Rest[1]);
  assign {controlled_buffer_7_out, MemAddr, RegAddr1} = _3_out ? {Rest[13:10], RegAddr2, RegAddr1} : 12'bz;  // Controlled_Buffer controlled_buffer_7
  and _4 (_4_out, Rest[0], Rest[1]);
  assign {controlled_buffer_8_out, RegAddr1} = _4_out ? {Rest[13:10], RegAddr2, RegAddr1} : 12'bz;  // Controlled_Buffer controlled_buffer_8
  assign WrtRegData = LAC_out ? ReadMem : 8'bz;  // Controlled_Buffer controlled_buffer_9
  Adder #(.width(16)) adder_3 (.a(pcout), .b(16'h4), .out(adder_3_out));  // open: cin, cout
  Multiplexer #(.width(16), .enable("false")) multiplexer_3 (
    .in0(pcout), .in1(pcin), .out(multiplexer_3_out), .sel(pcenable));
  Multiplexer #(.enable("false")) multiplexer_4 (.in0(1'b0), .in1(1'b1), .out(multiplexer_4_out), .sel(EnableReadReg));
  assign WrtAddrreg = _3_out ? RegAddr1 : 4'bz;  // Controlled_Buffer controlled_buffer_10
  Adder adder_4 (.a(RegData1), .b(ReadMem), .out(WrtRegData));  // open: cin, cout
  assign WrtAddrreg = _4_out ? RegAddr1 : 4'bz;  // Controlled_Buffer controlled_buffer_11
  Adder adder_5 (.a(RegData1), .b(ReadMem), .out(WrtRegData));  // open: cin, cout
  // Adder #(.width(16)) adder_6: pin names not known; wires that end beside it: controlled_buffer_8_out[7:4], adder_3_out, MemAddr
  Register #(.width(16)) PC (.D(adder_7_out), .Q(pcout), .clk(CLK), .clr(RESET));  // open: en
  Adder #(.width(16)) adder_7 (.a(16'h4), .b(multiplexer_3_out), .out(adder_7_out));  // open: cin, cout
  registers registers_1 (
    .Read_Register_1(RegAddr1), .Read_Register_2(RegAddr2), .Write_Register(WrtAddrreg),
    .Write_Data(WrtRegData), .Read_Data_1(RegData1), .Read_Data_2(RegData2), .clk(CLK), .reset(RESET),
    .Write(multiplexer_4_out));
  or or_1 (EnableReadMem, _3_out, LAC_out, _4_out);

  // Other names for the same wires on the sheet: Rest[9:2] = {RegAddr2, RegAddr1};
  //   typeofAdd[11:0] = {Rest[13:10], RegAddr2, RegAddr1}; EnableWrtReg = EnableReadReg

  // Notes on the sheet:
  //   Mnemonic
  //   ADD X
  //   JMP X
  //   Explanation
  //   ADD rs, rf
  //   ADD rs, #cte
  //   ADD rs, (rf)
  //   ADD rs, dir
  //   PC to X
  //   OPCODE
  //   00||rs||cte||01
  //   00||rs||dir||11
  //   10||desp
  //   00||rs||rf||XXXX||00
  //   00||rs||rf||XXXX||10
  //   PC INPUT SELECTOR
  //   Cant connect this
endmodule

module ControlUnit (
  input  [15:0] in_1
);
endmodule

module BitSplitter (
  input  [15:0] in_1,
  output [12:0] OUTPUT
);

  wire rshift_out;
  wire [12:0] shifter_1_out;

  // AND_Gate ldr has open pins: in0=in_1[13], in1=in_1[14], in2=in_1[15], out=open
  // AND_Gate str has open pins: in0=in_1[13], in1=in_1[14], in2=in_1[15], out=open
  // AND_Gate add has open pins: in0=in_1[13], in1=in_1[14], in2=in_1[15], out=open
  // AND_Gate and has open pins: in0=in_1[13], in1=in_1[14], in2=in_1[15], out=open
  // AND_Gate jmp has open pins: in0=in_1[13], in1=in_1[14], in2=in_1[15], out=open
  // AND_Gate jmpz has open pins: in0=in_1[13], in1=in_1[14], in2=in_1[15], out=open
  // AND_Gate cmp has open pins: in0=in_1[13], in1=in_1[14], in2=in_1[15], out=open
  and rshift (rshift_out, in_1[13], in_1[14], in_1[15]);
  Shifter #(.width(13)) shifter_1 (.in(in_1[12:0]), .\dist (4'b0001), .out(shifter_1_out));
  assign OUTPUT = rshift_out ? shifter_1_out : 13'bz;  // Controlled_Buffer controlled_buffer_1

  // Other names for the same wires on the sheet: Rest[12:0] = in_1[12:0]; out[12:0] = OUTPUT
endmodule

module Mem16 (
  input  Write,
  input  [3:0] Address,
  input  [15:0] Write_Data,
  input  clk,
  input  reset,
  input  Read,
  output [7:0] Read_Data
);

  wire [9:0] bitselector_1_out;
  wire [15:4] undriven;
  wire [15:8] ram_1_data;

  BitSelector #(.width(16), .group(10)) bitselector_1 (.in({undriven, Address}), .out(bitselector_1_out), .sel(1'b0));
  RAM #(.dataWidth(16), .bus("separate")) ram_1 (
    .addr(bitselector_1_out[9:2]), .din(Write_Data), .data({ram_1_data, Read_Data}), .str(Write), .sel(1'b1),
    .clk(clk), .ld(Read), .clr(reset));
  // Pins of 8 and 16 bits meet at {ram_1_data, Read_Data}
  // Pins of 4 and 16 bits meet at {undriven, Address}
endmodule

module Instruction_memory (
  input  [15:0] Read_address,
  output [15:0] Instruction
);

  wire [7:0] bitselector_1_out;
  wire [15:14] undriven;

  BitSelector #(.width(16), .group(8)) bitselector_1 (
    .in({undriven, Read_address[15:2]}), .out(bitselector_1_out), .sel(1'b0));
  RAM #(.dataWidth(16), .bus("asynch")) ram_1 (
    .addr(bitselector_1_out), .data(Instruction), .sel(1'b1), .ld(1'b1), .clr(1'b0));
endmodule

module registers (
  input  clk,
  input  reset,
  input  [3:0] Read_Register_1,
  input  [3:0] Read_Register_2,
  input  [3:0] Write_Register,
  input  [7:0] Write_Data,
  input  Write,
  output [7:0] Read_Data_1,
  output [7:0] Read_Data_2
);

  wire decoder_1_out1, decoder_1_out2, decoder_1_out3, decoder_1_out4, decoder_1_out5, decoder_1_out6,
       decoder_1_out7, decoder_1_out8, decoder_1_out9, decoder_1_out10, decoder_1_out11, decoder_1_out12,
       decoder_1_out13, decoder_1_out14, decoder_1_out15, decoder_1_out16, decoder_1_out17, decoder_1_out18,
       decoder_1_out19, decoder_1_out20, decoder_1_out21, decoder_1_out22, decoder_1_out23, decoder_1_out24,
       decoder_1_out25, decoder_1_out26, decoder_1_out27, decoder_1_out28, decoder_1_out29, decoder_1_out30,
       decoder_1_out31;
  wire [4:4] undriven;
  wire [15:0] R1_q, R2_q, R3_q, R4_q, R5_q, R6_q, R7_q, R8_q, R9_q, R10_q, R11_q, R12_q, R13_q, R14_q, R15_q,
       R16_q, R17_q, R18_q, R19_q, R20_q, R21_q, R22_q, R23_q, R24_q, R25_q, R26_q, R27_q, R28_q, R29_q,
       R30_q, R31_q;
  wire [15:8] undriven_2;

  Decoder #(.select(5), .disabled(0)) decoder_1 (
    .out1(decoder_1_out1), .out2(decoder_1_out2), .out3(decoder_1_out3), .out4(decoder_1_out4),
    .out5(decoder_1_out5), .out6(decoder_1_out6), .out7(decoder_1_out7), .out8(decoder_1_out8),
    .out9(decoder_1_out9), .out10(decoder_1_out10), .out11(decoder_1_out11), .out12(decoder_1_out12),
    .out13(decoder_1_out13), .out14(decoder_1_out14), .out15(decoder_1_out15), .out16(decoder_1_out16),
    .out17(decoder_1_out17), .out18(decoder_1_out18), .out19(decoder_1_out19), .out20(decoder_1_out20),
    .out21(decoder_1_out21), .out22(decoder_1_out22), .out23(decoder_1_out23), .out24(decoder_1_out24),
    .out25(decoder_1_out25), .out26(decoder_1_out26), .out27(decoder_1_out27), .out28(decoder_1_out28),
    .out29(decoder_1_out29), .out30(decoder_1_out30), .out31(decoder_1_out31),
    .sel({undriven[4], Write_Register}), .en(Write));  // open: out0
  Register #(.width(16)) R1 (.D({undriven_2, Write_Data}), .en(decoder_1_out1), .Q(R1_q), .clk(clk), .clr(reset));
  Register #(.width(16)) R2 (.D({undriven_2, Write_Data}), .en(decoder_1_out2), .Q(R2_q), .clk(clk), .clr(reset));
  Register #(.width(16)) R3 (.D({undriven_2, Write_Data}), .en(decoder_1_out3), .Q(R3_q), .clk(clk), .clr(reset));
  Register #(.width(16)) R4 (.D({undriven_2, Write_Data}), .en(decoder_1_out4), .Q(R4_q), .clk(clk), .clr(reset));
  Register #(.width(16)) R5 (.D({undriven_2, Write_Data}), .en(decoder_1_out5), .Q(R5_q), .clk(clk), .clr(reset));
  Register #(.width(16)) R6 (.D({undriven_2, Write_Data}), .en(decoder_1_out6), .Q(R6_q), .clk(clk), .clr(reset));
  Register #(.width(16)) R7 (.D({undriven_2, Write_Data}), .en(decoder_1_out7), .Q(R7_q), .clk(clk), .clr(reset));
  Register #(.width(16)) R8 (.D({undriven_2, Write_Data}), .en(decoder_1_out8), .Q(R8_q), .clk(clk), .clr(reset));
  Register #(.width(16)) R9 (.D({undriven_2, Write_Data}), .en(decoder_1_out9), .Q(R9_q), .clk(clk), .clr(reset));
  Register #(.width(16)) R10 (.D({undriven_2, Write_Data}), .en(decoder_1_out10), .Q(R10_q), .clk(clk), .clr(reset));
  Register #(.width(16)) R11 (.D({undriven_2, Write_Data}), .en(decoder_1_out11), .Q(R11_q), .clk(clk), .clr(reset));
  Register #(.width(16)) R12 (.D({undriven_2, Write_Data}), .en(decoder_1_out12), .Q(R12_q), .clk(clk), .clr(reset));
  Register #(.width(16)) R13 (.D({undriven_2, Write_Data}), .en(decoder_1_out13), .Q(R13_q), .clk(clk), .clr(reset));
  Register #(.width(16)) R14 (.D({undriven_2, Write_Data}), .en(decoder_1_out14), .Q(R14_q), .clk(clk), .clr(reset));
  Register #(.width(16)) R15 (.D({undriven_2, Write_Data}), .en(decoder_1_out15), .Q(R15_q), .clk(clk), .clr(reset));
  Register #(.width(16)) R16 (.D({undriven_2, Write_Data}), .en(decoder_1_out16), .Q(R16_q), .clk(clk), .clr(reset));
  Register #(.width(16)) R17 (.D({undriven_2, Write_Data}), .en(decoder_1_out17), .Q(R17_q), .clk(clk), .clr(reset));
  Register #(.width(16)) R18 (.D({undriven_2, Write_Data}), .en(decoder_1_out18), .Q(R18_q), .clk(clk), .clr(reset));
  Register #(.width(16)) R19 (.D({undriven_2, Write_Data}), .en(decoder_1_out19), .Q(R19_q), .clk(clk), .clr(reset));
  Register #(.width(16)) R20 (.D({undriven_2, Write_Data}), .en(decoder_1_out20), .Q(R20_q), .clk(clk), .clr(reset));
  Register #(.width(16)) R21 (.D({undriven_2, Write_Data}), .en(decoder_1_out21), .Q(R21_q), .clk(clk), .clr(reset));
  Register #(.width(16)) R22 (.D({undriven_2, Write_Data}), .en(decoder_1_out22), .Q(R22_q), .clk(clk), .clr(reset));
  Register #(.width(16)) R23 (.D({undriven_2, Write_Data}), .en(decoder_1_out23), .Q(R23_q), .clk(clk), .clr(reset));
  Register #(.width(16)) R24 (.D({undriven_2, Write_Data}), .en(decoder_1_out24), .Q(R24_q), .clk(clk), .clr(reset));
  Register #(.width(16)) R25 (.D({undriven_2, Write_Data}), .en(decoder_1_out25), .Q(R25_q), .clk(clk), .clr(reset));
  Register #(.width(16)) R26 (.D({undriven_2, Write_Data}), .en(decoder_1_out26), .Q(R26_q), .clk(clk), .clr(reset));
  Register #(.width(16)) R27 (.D({undriven_2, Write_Data}), .en(decoder_1_out27), .Q(R27_q), .clk(clk), .clr(reset));
  Register #(.width(16)) R28 (.D({undriven_2, Write_Data}), .en(decoder_1_out28), .Q(R28_q), .clk(clk), .clr(reset));
  Register #(.width(16)) R29 (.D({undriven_2, Write_Data}), .en(decoder_1_out29), .Q(R29_q), .clk(clk), .clr(reset));
  Register #(.width(16)) R30 (.D({undriven_2, Write_Data}), .en(decoder_1_out30), .Q(R30_q), .clk(clk), .clr(reset));
  Register #(.width(16)) R31 (.D({undriven_2, Write_Data}), .en(decoder_1_out31), .Q(R31_q), .clk(clk), .clr(reset));
  // Multiplexer #(.select(4), .width(16), .enable("false")) multiplexer_1: pin names not known; wires that end beside it: R5_q, R6_q, R7_q, R8_q, R9_q, R10_q, R11_q, R12_q, R13_q, R14_q, R15_q, R16_q, R17_q, R18_q, R19_q, R20_q, R21_q, R22_q, R23_q, R24_q, R25_q, R26_q, R27_q, Read_Data_1
  // Multiplexer #(.select(4), .width(16), .enable("false")) multiplexer_2: pin names not known; wires that end beside it: R5_q, R6_q, R7_q, R8_q, R9_q, R10_q, R11_q, R12_q, R13_q, R14_q, R15_q, R16_q, R17_q, R18_q, R19_q, R20_q, R21_q, R22_q, R23_q, R24_q, R25_q, R26_q, R27_q, Read_Data_2
  // Pins of 8 and 16 bits meet at {undriven_2, Write_Data}
  // Pins of 4 and 5 bits meet at {undriven[4], Write_Register}
endmodule
