// Logisim project 16 Bit.circ as structural Verilog: 5 circuits, main circuit main
module main (
  input  RESET,
  output Zero
);

  wire add_out, and_out, CLK, cmp_out, EnableReadMem, EnableWRTMem, ldm_out, multiplexer_2_out,
       multiplexer_3_out, pcenable, rshift_out;
  wire [12:0] controlled_buffer_1_out, controlled_buffer_3_out, controlled_buffer_7_out,
       controlled_buffer_8_out, controlled_buffer_9_out, Rest;
  wire [15:0] acin, acout, adder_1_out, adder_2_out, and_2_out, bit_extender_4_out, MemAddr, MemWrtData,
       multiplexer_1_out, not_1_out, pcin, pcout, ReadMem, shifter_1_out;
  wire [15:13] instruction_memory_1_instruction;

  Instruction_memory instruction_memory_1 (
    .Read_address(pcout), .Instruction({instruction_memory_1_instruction, Rest}));
  and ldm (ldm_out, ~instruction_memory_1_instruction[13], ~instruction_memory_1_instruction[14], ~instruction_memory_1_instruction[15]);  // AND_Gate
  and add (add_out, ~instruction_memory_1_instruction[13], instruction_memory_1_instruction[14], ~instruction_memory_1_instruction[15]);  // AND_Gate
  and \and  (and_out, instruction_memory_1_instruction[13], instruction_memory_1_instruction[14], ~instruction_memory_1_instruction[15]);  // AND_Gate
  and stm (EnableWRTMem, instruction_memory_1_instruction[13], ~instruction_memory_1_instruction[14], ~instruction_memory_1_instruction[15]);  // AND_Gate
  assign controlled_buffer_1_out = ldm_out ? Rest : 13'bz;  // Controlled_Buffer controlled_buffer_1
  assign MemAddr = {{3{1'b0}}, controlled_buffer_1_out};  // Bit_Extender bit_extender_1
  Adder #(.width(16)) adder_1 (.a(acout), .b(ReadMem), .out(adder_1_out));  // open: cin, cout
  assign acin = and_out ? and_2_out : 16'bz;  // Controlled_Buffer controlled_buffer_2
  assign and_2_out = acout & ReadMem;  // AND_Gate and_2, 16 bits wide
  assign controlled_buffer_3_out = EnableWRTMem ? Rest : 13'bz;  // Controlled_Buffer controlled_buffer_3
  assign MemAddr = {{3{1'b0}}, controlled_buffer_3_out};  // Bit_Extender bit_extender_2
  assign acin = add_out ? adder_1_out : 16'bz;  // Controlled_Buffer controlled_buffer_4
  assign acin = ldm_out ? ReadMem : 16'bz;  // Controlled_Buffer controlled_buffer_5
  assign MemWrtData = EnableWRTMem ? acout : 16'bz;  // Controlled_Buffer controlled_buffer_6
  Clock u_CLK (.out(CLK));
  or or_1 (EnableReadMem, ldm_out, add_out, and_out);
  Counter #(.width(16), .max('hffff)) ACum (.D(acin), .Q(acout), .clk(CLK), .clr(RESET));  // open: load, count, carry
  and jmp (pcenable, ~instruction_memory_1_instruction[13], ~instruction_memory_1_instruction[14], instruction_memory_1_instruction[15]);  // AND_Gate
  and jmpz (pcenable, instruction_memory_1_instruction[13], ~instruction_memory_1_instruction[14], instruction_memory_1_instruction[15]);  // AND_Gate
  and cmp (cmp_out, ~instruction_memory_1_instruction[13], instruction_memory_1_instruction[14], instruction_memory_1_instruction[15]);  // AND_Gate
  and rshift (rshift_out, instruction_memory_1_instruction[13], instruction_memory_1_instruction[14], instruction_memory_1_instruction[15]);
  Adder #(.width(16)) adder_2 (.a(pcin), .b(16'h4), .out(adder_2_out));  // open: cin, cout
  assign controlled_buffer_7_out = pcenable ? Rest : 13'bz;  // Controlled_Buffer controlled_buffer_7
  assign pcin = {{3{1'b0}}, controlled_buffer_7_out};  // Bit_Extender bit_extender_3
  assign controlled_buffer_8_out = Zero ? Rest : 13'bz;  // Controlled_Buffer controlled_buffer_8
  assign controlled_buffer_9_out = pcenable ? controlled_buffer_8_out : 13'bz;  // Controlled_Buffer controlled_buffer_9
  assign not_1_out = ~bit_extender_4_out;  // NOT_Gate not_1, 16 bits wide
  assign bit_extender_4_out = {{3{1'b0}}, Rest};  // Bit_Extender bit_extender_4
  Shifter #(.width(16)) shifter_1 (.in(acout), .\dist (4'b0001), .out(shifter_1_out));
  assign acin = rshift_out ? shifter_1_out : 16'bz;  // Controlled_Buffer controlled_buffer_10
  Multiplexer #(.width(16), .enable("false")) multiplexer_1 (
    .in0(adder_2_out), .in1(pcin), .out(multiplexer_1_out), .sel(pcenable));
  assign pcin = {{3{1'b0}}, controlled_buffer_9_out};  // Bit_Extender bit_extender_5
  assign acin = cmp_out ? not_1_out : 16'bz;  // Controlled_Buffer controlled_buffer_11
  Register #(.width(16)) PC (.D(multiplexer_1_out), .Q(pcout), .clk(CLK), .clr(RESET));  // open: en
  Mem16 mem16_1 (
    .Address(MemAddr), .Write_Data(MemWrtData), .Read_Data(ReadMem), .Write(multiplexer_2_out), .clk(CLK),
    .reset(RESET), .Read(multiplexer_3_out));
  Multiplexer #(.enable("false")) multiplexer_2 (.in0(1'b0), .in1(1'b1), .out(multiplexer_2_out), .sel(EnableWRTMem));
  Multiplexer #(.enable("false")) multiplexer_3 (.in0(1'b0), .in1(1'b1), .out(multiplexer_3_out), .sel(EnableReadMem));

  // Notes on the sheet:
  //   Mnemonic
  //   LOAD X
  //   STORE X
  //   ADD X
  //   AND X
  //   JMP X
  //   JMPZ X
  //   CMP X
  //   RSHIFT X
  //   Explanation
  //   Mem(x) to ACum.
  //   ACum to Mem(x) 
  //   ACum = ACum + Mem(x) 
  //   ACum = ACum ^ Mem(x) 
  //   PC to X
  //   PC to X if 0 flag 
  //   Complementation of AC
  //   RightShift
  //   OPCODE
  //   000
  //   001
  //   010
  //   011
  //   100
  //   101
  //   110
  //   111
  //   What OP toogles zero flag?
  //   PC INPUT SELECTOR
endmodule

module ControlUnit (
  input  [15:0] in_1
);
endmodule

module BitSplitter (
  input  [15:0] in_1,
  output [12:0] OUTPUT
);

  wire rshift_out;
  wire [12:0] shifter_1_out;

  // AND_Gate ldr has open pins: in0=in_1[13], in1=in_1[14], in2=in_1[15], out=open
  // AND_Gate str has open pins: in0=in_1[13], in1=in_1[14], in2=in_1[15], out=open
  // AND_Gate add has open pins: in0=in_1[13], in1=in_1[14], in2=in_1[15], out=open
  // AND_Gate and has open pins: in0=in_1[13], in1=in_1[14], in2=in_1[15], out=open
  // AND_Gate jmp has open pins: in0=in_1[13], in1=in_1[14], in2=in_1[15], out=open
  // AND_Gate jmpz has open pins: in0=in_1[13], in1=in_1[14], in2=in_1[15], out=open
  // AND_Gate cmp has open pins: in0=in_1[13], in1=in_1[14], in2=in_1[15], out=open
  and rshift (rshift_out, in_1[13], in_1[14], in_1[15]);
  Shifter #(.width(13)) shifter_1 (.in(in_1[12:0]), .\dist (4'b0001), .out(shifter_1_out));
  assign OUTPUT = rshift_out ? shifter_1_out : 13'bz;  // Controlled_Buffer controlled_buffer_1

  // Other names for the same wires on the sheet: Rest[12:0] = in_1[12:0]; out[12:0] = OUTPUT
endmodule

module Mem16 (
  input  Write,
  input  [15:0] Address,
  input  [15:0] Write_Data,
  input  clk,
  input  reset,
  input  Read,
  output [15:0] Read_Data
);

  wire [9:0] bitselector_1_out;

  BitSelector #(.width(16), .group(10)) bitselector_1 (.in(Address), .out(bitselector_1_out), .sel(1'b0));
  RAM #(.dataWidth(16), .bus("separate")) ram_1 (
    .addr(bitselector_1_out[9:2]), .din(Write_Data), .data(Read_Data), .str(Write), .sel(1'b1), .clk(clk),
    .ld(Read), .clr(reset));
endmodule

module Instruction_memory (
  input  [15:0] Read_address,
  output [15:0] Instruction
);

  wire [7:0] bitselector_1_out;
  wire [15:14] undriven;

  BitSelector #(.width(16), .group(8)) bitselector_1 (
    .in({undriven, Read_address[15:2]}), .out(bitselector_1_out), .sel(1'b0));
  RAM #(.dataWidth(16), .bus("asynch")) ram_1 (
    .addr(bitselector_1_out), .data(Instruction), .sel(1'b1), .ld(1'b1), .clr(1'b0));
endmodule
