// Logisim project Computer.circ as structural Verilog: 18 circuits, main circuit 4bitAdder
module MainOP (
  input  CLK,
  input  SET0,
  output out_3,
  output [7:0] out_4
);

  wire alu_1_carry_out, alu_1_sign, alu_1_zero_flag, and_1_out, and_2_out, and_3_out, CLEAR_out,
       controlled_buffer_4_out, d_ff_1_q, decoder_1_out0, decoder_1_out1, decoder_1_out2, decoder_1_out3,
       decoder_1_out4, decoder_1_out5, decoder_1_out6, MOV_out, xnor_1_out;
  wire [2:0] d_ff_3_q;
  wire [7:0] controlled_buffer_5_out, counter_1_q, multiplexer_1_out, multiplexer_2_out, multiplexer_3_out,
       multiplexer_4_out, register_1_q, register_2_q;
  wire [9:9] not_1_out;
  wire [13:0] undriven;
  wire [20:0] controlled_buffer_1_out;

  Register register_1 (.D(out_4), .en(controlled_buffer_1_out[9]), .Q(register_1_q), .clk(CLK), .clr(SET0));
  Register register_2 (.D(out_4), .en(controlled_buffer_1_out[10]), .Q(register_2_q), .clk(CLK), .clr(SET0));
  assign controlled_buffer_1_out = CLEAR_out ? 21'h20000 : 21'bz;  // Controlled_Buffer controlled_buffer_1
  assign controlled_buffer_1_out = d_ff_1_q ? {7'b0101100, undriven} : 21'bz;  // Controlled_Buffer controlled_buffer_2
  D_Flip_Flop d_ff_1 (.clk(CLK), .D(controlled_buffer_4_out), .Q(d_ff_1_q), .preset(SET0));  // open: Qn, en, reset
  Multiplexer_part #(.select(3), .width(8), .enable("false")) multiplexer_1 (
    .in0(register_1_q), .in1(register_2_q), .in2(controlled_buffer_5_out), .out(multiplexer_1_out),
    .sel(controlled_buffer_1_out[5:3]));  // open: in3, in4, in5, in6, in7
  Multiplexer_part #(.select(3), .width(8), .enable("false")) multiplexer_2 (
    .in0(register_1_q), .in1(register_2_q), .in2({8{1'b0}}), .out(multiplexer_2_out),
    .sel(controlled_buffer_1_out[2:0]));  // open: in3, in4, in5, in6, in7
  and and_1 (and_1_out, d_ff_1_q, ~controlled_buffer_4_out);  // AND_Gate
  and and_2 (and_2_out, MOV_out, d_ff_1_q);
  xnor xnor_1 (xnor_1_out, multiplexer_4_out[0], multiplexer_4_out[1]);
  and and_3 (and_3_out, and_2_out, ~xnor_1_out);  // AND_Gate
  assign controlled_buffer_1_out = and_3_out ? {10'h160, multiplexer_4_out[1], not_1_out[9], 3'b100, multiplexer_4_out[0], 2'b00, multiplexer_4_out[0], 2'b00} : 21'bz;  // Controlled_Buffer controlled_buffer_3
  Decoder #(.select(3), .enable("false")) decoder_1 (
    .out0(decoder_1_out0), .out1(decoder_1_out1), .out2(decoder_1_out2), .out3(decoder_1_out3),
    .out4(decoder_1_out4), .out5(decoder_1_out5), .out6(decoder_1_out6), .sel(controlled_buffer_1_out[8:6]));  // open: out7
  Counter counter_1 (
    .load(controlled_buffer_1_out[15]), .D(out_4), .count(controlled_buffer_1_out[16]), .Q(counter_1_q),
    .clk(CLK), .clr(SET0));  // open: carry
  D_Flip_Flop d_ff_2 (.clk(CLK), .D(and_1_out), .reset(SET0));  // open: Q, Qn, preset, en
  assign controlled_buffer_4_out = and_3_out ? 1'b1 : 1'bz;  // Controlled_Buffer controlled_buffer_4
  not not_1 (not_1_out[9], multiplexer_4_out[1]);
  D_Flip_Flop d_ff_3 (
    .clk(CLK), .D(alu_1_carry_out), .Q(d_ff_3_q[0]), .en(controlled_buffer_1_out[13]), .reset(SET0));  // open: Qn, preset
  ALU alu_1 (
    .RSL(decoder_1_out0), .LSR(decoder_1_out1), .XOR(decoder_1_out2), .OR(decoder_1_out3),
    .AND(decoder_1_out4), .Add(decoder_1_out5), .Input_B(multiplexer_1_out), .Input_A(multiplexer_2_out),
    .Output(out_4), .Carry_out(alu_1_carry_out), .Sub(decoder_1_out6), .Zero_Flag(alu_1_zero_flag),
    .Sign(alu_1_sign));
  Multiplexer_part #(.select(3), .width(8), .enable("false")) multiplexer_3 (
    .in0(multiplexer_1_out), .in1(multiplexer_2_out), .in2(counter_1_q), .out(multiplexer_3_out),
    .sel(controlled_buffer_1_out[20:18]));  // open: in3, in4, in5, in6, in7
  D_Flip_Flop d_ff_4 (
    .clk(CLK), .D(alu_1_zero_flag), .Q(d_ff_3_q[1]), .en(controlled_buffer_1_out[12]), .reset(SET0));  // open: Qn, preset
  D_Flip_Flop d_ff_5 (
    .clk(CLK), .D(alu_1_sign), .Q(d_ff_3_q[2]), .en(controlled_buffer_1_out[11]), .reset(SET0));  // open: Qn, preset
  assign controlled_buffer_5_out = controlled_buffer_1_out[14] ? out_4 : 8'bz;  // Controlled_Buffer controlled_buffer_5
  RAM_part ram_1 (
    .addr(multiplexer_3_out), .data(controlled_buffer_5_out), .sel(1'b1), .clk(CLK),
    .ld(controlled_buffer_1_out[17]));  // open: clr
  // Probe on controlled_buffer_5_out
  Multiplexer_part #(.width(8), .enable("false")) multiplexer_4 (
    .in0(controlled_buffer_5_out), .in1({8{1'b1}}), .out(multiplexer_4_out), .sel(SET0));
  and CLEAR (CLEAR_out, multiplexer_4_out[0], multiplexer_4_out[1], multiplexer_4_out[2], multiplexer_4_out[3], multiplexer_4_out[5], multiplexer_4_out[6], multiplexer_4_out[7], multiplexer_4_out[4]);
  and MOV (MOV_out, ~multiplexer_4_out[4], ~multiplexer_4_out[5], ~multiplexer_4_out[6], ~multiplexer_4_out[7]);  // AND_Gate
  // also tied to GND on the sheet: multiplexer_4_out[0]

  // Notes on the sheet:
  //   Data
  //   REG 1
  //   REG 2
  //   2PhaseClk
  //   SELECT OP
  //   COUNT
  //   LOAD RAM MEM TO OUTPUT
  //   RAM INPUT SELECTOR
  //   MOV ENABLED (0/1)
  //   DATA STREAM (8 BITS)
  //   SELECT INPUT B
  //   SELECT INPUT A
  //   ENABLE REG1
  //   ENABLE REG2
  //   ENABLE FLAGS
  //   CTRL OUTPUT ALU
  //   LOAD COUNTER
  //   Phase 1
  //   memory bus
  //   INPUT A - ALU
  //   INPUT B -ALU
  //   INPUT A
  //   INPUT B
  //   COUNTER X
  //   SELECT OP
  //   INPUT REG&ALU
  //   Stop Phase
  //   CARRY
  //   ZERO
  //   Select Address
  //   SIGN
  //   CTRL OUTPUT ALU
  //   RAM
  //   MOV INSTRUCTION
  //   EnableA X
  //   EnableB X
  //   Select A XXX
  //   Select B 010
  //   AluOP ADD
  //   Flags 000
  //   EnableALU 0
  //   LoadCounter 0
  //   IncrementCounter 1
  //   SelectAdress 010
  //   LoadMem1
  //   FLAGS
  //   010 1 1 0 0 000 X X 100 010 XXX
  //   Set 0 if Clear
endmodule

module FullAdder (
  input  in_1,
  input  in_2,
  input  in_3,
  output Carry,
  output Sum
);

  wire a_b_out, a_c_out, b_c_out;

  and a_b (a_b_out, in_1, in_2);
  and a_c (a_c_out, in_1, in_3);
  and b_c (b_c_out, in_2, in_3);
  xor xor_1 (Sum, in_1, in_2, in_3);
  or or_1 (Carry, a_b_out, a_c_out, b_c_out);
endmodule

module _4bitAdder (
  input  [3:0] _4_Bit_Input,
  input  [3:0] _4_Bit_Input_B,
  input  Carry_input,
  output Carry,
  output [3:0] Output
);

  wire fulladder_2_carry, fulladder_3_carry, fulladder_4_carry;

  FullAdder fulladder_1 (
    .in_1(fulladder_2_carry), .in_2(_4_Bit_Input[3]), .in_3(_4_Bit_Input_B[3]), .Carry(Carry), .Sum(Output[3]));
  FullAdder fulladder_2 (
    .in_1(fulladder_3_carry), .in_2(_4_Bit_Input[2]), .in_3(_4_Bit_Input_B[2]), .Carry(fulladder_2_carry),
    .Sum(Output[2]));
  FullAdder fulladder_3 (
    .in_1(fulladder_4_carry), .in_2(_4_Bit_Input[1]), .in_3(_4_Bit_Input_B[1]), .Carry(fulladder_3_carry),
    .Sum(Output[1]));
  FullAdder fulladder_4 (
    .in_1(Carry_input), .in_2(_4_Bit_Input[0]), .in_3(_4_Bit_Input_B[0]), .Carry(fulladder_4_carry),
    .Sum(Output[0]));
endmodule

module Flipper (
  input  in_1,
  input  in_2,
  input  in_3,
  input  in_4,
  input  in_5,
  output out_6,
  output out_7,
  output out_8,
  output out_9
);

  xor xor_1 (out_6, in_1, in_5);
  xor xor_2 (out_7, in_2, in_5);
  xor xor_3 (out_8, in_3, in_5);
  xor xor_4 (out_9, in_4, in_5);
endmodule

module _8bitAdder (
  input  [7:0] in_1,
  input  [7:0] in_2,
  input  in_3,
  output out_4,
  output [7:0] out_5
);

  wire n4bitadder_2_carry;

  _4bitAdder u_4bitadder_1 (
    ._4_Bit_Input(in_1[7:4]), ._4_Bit_Input_B(in_2[7:4]), .Carry_input(n4bitadder_2_carry),
    .Output(out_5[7:4]), .Carry(out_4));
  _4bitAdder u_4bitadder_2 (
    ._4_Bit_Input(in_1[3:0]), ._4_Bit_Input_B(in_2[3:0]), .Carry_input(in_3), .Output(out_5[3:0]),
    .Carry(n4bitadder_2_carry));
endmodule

module AdderNoLogicGates (
  input  [7:0] Input_a,
  input  [7:0] Input_B,
  input  Sign,
  output Carry_out,
  output [7:0] Output
);

  wire [7:0] bit_extender_1_out, xor_1_out;

  assign bit_extender_1_out = {{7{Sign}}, Sign};  // Bit_Extender bit_extender_1
  assign xor_1_out = Input_B ^ bit_extender_1_out;  // XOR_Gate xor_1, 8 bits wide
  Adder adder_1 (.a(Input_a), .b(xor_1_out), .out(Output), .cin(Sign), .cout(Carry_out));
endmodule

module ALU (
  input  RSL,
  input  LSR,
  input  XOR,
  input  OR,
  input  AND,
  input  Add,
  input  Sub,
  input  [7:0] Input_B,
  input  [7:0] Input_A,
  output [7:0] Output,
  output Zero_Flag,
  output Sign,
  output Carry_out
);

  wire adder_1_cout, leftshift_1_carry, or_1_out, rightshift_1_carry;
  wire [7:0] adder_1_out, and_1_out, bit_extender_1_out, leftshift_1_out_2, or_2_out, rightshift_1_out_3,
       xor_1_out, xor_2_out;

  assign bit_extender_1_out = {{7{Sub}}, Sub};  // Bit_Extender bit_extender_1
  or or_1 (or_1_out, Add, Sub);
  assign xor_1_out = bit_extender_1_out ^ Input_B;  // XOR_Gate xor_1, 8 bits wide
  Adder adder_1 (.a(xor_1_out), .b(Input_A), .out(adder_1_out), .cin(Sub), .cout(adder_1_cout));
  assign and_1_out = Input_B & Input_A;  // AND_Gate and_1, 8 bits wide
  assign or_2_out = Input_B | Input_A;  // OR_Gate or_2, 8 bits wide
  assign xor_2_out = Input_B ^ Input_A;  // XOR_Gate xor_2, 8 bits wide
  LeftShift leftshift_1 (.in_1(Input_A), .out_2(leftshift_1_out_2), .Carry(leftshift_1_carry));
  RightShift rightshift_1 (.in_1(Input_A), .out_3(rightshift_1_out_3), .Carry(rightshift_1_carry));
  assign Output = or_1_out ? adder_1_out : 8'bz;  // Controlled_Buffer A
  assign Output = AND ? and_1_out : 8'bz;  // Controlled_Buffer B
  assign Carry_out = LSR ? leftshift_1_carry : 1'bz;  // Controlled_Buffer controlled_buffer_1
  assign Carry_out = RSL ? rightshift_1_carry : 1'bz;  // Controlled_Buffer controlled_buffer_2
  assign Output = OR ? or_2_out : 8'bz;  // Controlled_Buffer C
  assign Output = XOR ? xor_2_out : 8'bz;  // Controlled_Buffer D
  assign Output = LSR ? leftshift_1_out_2 : 8'bz;  // Controlled_Buffer E
  assign Output = RSL ? rightshift_1_out_3 : 8'bz;  // Controlled_Buffer F
  assign Carry_out = or_1_out ? adder_1_cout : 1'bz;  // Controlled_Buffer controlled_buffer_3
  nor nor_1 (Zero_Flag, Output[0], Output[1], Output[2], Output[3], Output[4], Output[5], Output[6], Output[7]);

  assign Sign = Output[7];
endmodule

module LeftShift (
  input  [7:0] in_1,
  output [7:0] out_2,
  output Carry
);


  assign Carry = in_1[7];
  assign out_2 = {in_1[6:0], 1'b0};
endmodule

module RightShift (
  input  [7:0] in_1,
  output Carry,
  output [7:0] out_3
);


  assign Carry = in_1[0];
  assign out_3 = {1'b0, in_1[7:1]};
endmodule

// ManualRegisters
module WorkingwithRegisters (
  input  [7:0] in_1,
  input  in_2,
  input  in_3,
  input  in_4,
  input  in_5,
  input  in_6,
  input  in_7,
  input  in_8,
  input  in_9,
  input  in_10,
  input  in_11,
  input  in_12,
  input  in_13,
  input  in_14,
  input  in_15,
  input  in_16,
  input  in_17,
  output [7:0] out_18,
  output out_19
);

  wire clock_1_out;
  wire [7:0] controlled_buffer_1_out, controlled_buffer_2_out, register_1_q, register_2_q;

  Clock clock_1 (.out(clock_1_out));
  assign controlled_buffer_1_out = in_10 ? {8{1'b0}} : 8'bz;  // Controlled_Buffer controlled_buffer_1
  assign controlled_buffer_2_out = in_14 ? register_1_q : 8'bz;  // Controlled_Buffer controlled_buffer_2
  Register register_1 (.D(out_18), .en(in_11), .Q(register_1_q), .clk(clock_1_out), .clr(in_13));
  Register register_2 (.D(out_18), .en(in_12), .Q(register_2_q), .clk(clock_1_out), .clr(in_13));
  assign controlled_buffer_2_out = in_2 ? in_1 : 8'bz;  // Controlled_Buffer controlled_buffer_3
  assign controlled_buffer_1_out = in_15 ? register_1_q : 8'bz;  // Controlled_Buffer controlled_buffer_4
  assign controlled_buffer_2_out = in_16 ? register_2_q : 8'bz;  // Controlled_Buffer controlled_buffer_5
  assign controlled_buffer_1_out = in_17 ? register_2_q : 8'bz;  // Controlled_Buffer controlled_buffer_6
  // ALU alu_1: pin names not known; wires that end beside it: controlled_buffer_2_out, controlled_buffer_1_out, in_3, in_4, in_5, in_6, in_7, in_8, in_9, out_18, out_19
endmodule

module RS_Flip_Flop (
  input  Set,
  input  Enable,
  input  _1,
  output Output
);

  wire and_1_out, and_2_out, nor_1_out, not_1_out, or_1_out;

  not not_1 (not_1_out, Set);
  and and_1 (and_1_out, Set, Enable);
  and and_2 (and_2_out, Enable, not_1_out);
  or or_1 (or_1_out, and_2_out, _1);
  nor nor_1 (nor_1_out, and_1_out, Output);
  nor nor_2 (Output, nor_1_out, or_1_out);
endmodule

module RAM (
  input  in_1,
  input  [2:0] in_2,
  input  [7:0] in_3,
  input  read_write,
  input  in_5,
  input  in_6,
  output [7:0] out_7
);

  wire and_1_out, and_2_out, and_3_out, and_4_out, and_5_out, and_6_out, and_7_out, and_8_out, and_9_out,
       and_10_out, and_11_out, and_12_out, and_13_out, and_14_out, and_15_out, and_16_out, decoder_1_out0,
       decoder_1_out1, decoder_1_out2, decoder_1_out3, decoder_1_out4, decoder_1_out5, decoder_1_out6,
       decoder_1_out7;
  wire [7:0] register_1_q, register_2_q, register_3_q, register_4_q, register_5_q, register_6_q,
       register_7_q, register_8_q;

  Decoder #(.select(3)) decoder_1 (
    .out0(decoder_1_out0), .out1(decoder_1_out1), .out2(decoder_1_out2), .out3(decoder_1_out3),
    .out4(decoder_1_out4), .out5(decoder_1_out5), .out6(decoder_1_out6), .out7(decoder_1_out7), .sel(in_2),
    .en(in_1));
  and and_1 (and_1_out, ~read_write, decoder_1_out0);  // AND_Gate
  and and_2 (and_2_out, decoder_1_out0, read_write);
  and and_3 (and_3_out, ~read_write, decoder_1_out1);  // AND_Gate
  and and_4 (and_4_out, decoder_1_out1, read_write);
  and and_5 (and_5_out, ~read_write, decoder_1_out2);  // AND_Gate
  and and_6 (and_6_out, decoder_1_out2, read_write);
  and and_7 (and_7_out, ~read_write, decoder_1_out3);  // AND_Gate
  and and_8 (and_8_out, decoder_1_out3, read_write);
  and and_9 (and_9_out, ~read_write, decoder_1_out4);  // AND_Gate
  and and_10 (and_10_out, decoder_1_out4, read_write);
  and and_11 (and_11_out, ~read_write, decoder_1_out5);  // AND_Gate
  and and_12 (and_12_out, decoder_1_out5, read_write);
  and and_13 (and_13_out, ~read_write, decoder_1_out6);  // AND_Gate
  and and_14 (and_14_out, decoder_1_out6, read_write);
  and and_15 (and_15_out, ~read_write, decoder_1_out7);  // AND_Gate
  and and_16 (and_16_out, decoder_1_out7, read_write);
  Register register_1 (.D(out_7), .en(and_1_out), .Q(register_1_q), .clk(in_5));  // open: clr
  Register register_2 (.D(out_7), .en(and_3_out), .Q(register_2_q), .clk(in_5));  // open: clr
  Register register_3 (.D(out_7), .en(and_5_out), .Q(register_3_q), .clk(in_5));  // open: clr
  Register register_4 (.D(out_7), .en(and_7_out), .Q(register_4_q), .clk(in_5));  // open: clr
  Register register_5 (.D(out_7), .en(and_9_out), .Q(register_5_q), .clk(in_5));  // open: clr
  Register register_6 (.D(out_7), .en(and_11_out), .Q(register_6_q), .clk(in_5));  // open: clr
  Register register_7 (.D(out_7), .en(and_13_out), .Q(register_7_q), .clk(in_5));  // open: clr
  Register register_8 (.D(out_7), .en(and_15_out), .Q(register_8_q), .clk(in_5));  // open: clr
  assign out_7 = and_2_out ? register_1_q : 8'bz;  // Controlled_Buffer controlled_buffer_1
  assign out_7 = and_4_out ? register_2_q : 8'bz;  // Controlled_Buffer controlled_buffer_2
  assign out_7 = and_6_out ? register_3_q : 8'bz;  // Controlled_Buffer controlled_buffer_3
  assign out_7 = and_8_out ? register_4_q : 8'bz;  // Controlled_Buffer controlled_buffer_4
  assign out_7 = and_10_out ? register_5_q : 8'bz;  // Controlled_Buffer controlled_buffer_5
  assign out_7 = and_12_out ? register_6_q : 8'bz;  // Controlled_Buffer controlled_buffer_6
  assign out_7 = and_14_out ? register_7_q : 8'bz;  // Controlled_Buffer controlled_buffer_7
  assign out_7 = and_16_out ? register_8_q : 8'bz;  // Controlled_Buffer controlled_buffer_8
  assign out_7 = in_6 ? in_3 : 8'bz;  // Controlled_Buffer controlled_buffer_9
endmodule

module _2BitDecoder (
  input  Bit0,
  input  Bit1,
  input  Enable,
  output out_4,
  output out_5,
  output out_6,
  output out_7
);

  and and_1 (out_4, ~Bit0, Enable, ~Bit1);  // AND_Gate
  and and_2 (out_5, Bit0, Enable, ~Bit1);  // AND_Gate
  and and_3 (out_6, ~Bit0, Enable, Bit1);  // AND_Gate
  and and_4 (out_7, Bit0, Enable, Bit1);
endmodule

module _4BitDecoder (
  input  in_1,
  input  in_2,
  input  in_3,
  input  in_4,
  input  in_5
);

  wire n2bitdecoder_1_out_4, n2bitdecoder_1_out_5, n2bitdecoder_1_out_6, n2bitdecoder_1_out_7,
       n2bitdecoder_2_out_4, n2bitdecoder_2_out_5, n2bitdecoder_2_out_6, n2bitdecoder_2_out_7,
       n2bitdecoder_3_out_4, n2bitdecoder_3_out_5, n2bitdecoder_3_out_6, n2bitdecoder_3_out_7,
       n2bitdecoder_4_out_4, n2bitdecoder_4_out_5, n2bitdecoder_4_out_6, n2bitdecoder_4_out_7,
       n2bitdecoder_5_out_4, n2bitdecoder_5_out_5, n2bitdecoder_5_out_6, n2bitdecoder_5_out_7;

  _2BitDecoder u_2bitdecoder_1 (
    .Bit0(in_3), .Enable(in_5), .out_4(n2bitdecoder_1_out_4), .out_5(n2bitdecoder_1_out_5),
    .out_6(n2bitdecoder_1_out_6), .out_7(n2bitdecoder_1_out_7), .Bit1(in_4));
  _2BitDecoder u_2bitdecoder_2 (
    .Bit0(in_1), .Enable(n2bitdecoder_1_out_4), .out_4(n2bitdecoder_2_out_4), .out_5(n2bitdecoder_2_out_5),
    .out_6(n2bitdecoder_2_out_6), .out_7(n2bitdecoder_2_out_7), .Bit1(in_2));
  _2BitDecoder u_2bitdecoder_3 (
    .Bit0(in_1), .Enable(n2bitdecoder_1_out_5), .out_4(n2bitdecoder_3_out_4), .out_5(n2bitdecoder_3_out_5),
    .out_6(n2bitdecoder_3_out_6), .out_7(n2bitdecoder_3_out_7), .Bit1(in_2));
  _2BitDecoder u_2bitdecoder_4 (
    .Bit0(in_1), .Enable(n2bitdecoder_1_out_6), .out_4(n2bitdecoder_4_out_4), .out_5(n2bitdecoder_4_out_5),
    .out_6(n2bitdecoder_4_out_6), .out_7(n2bitdecoder_4_out_7), .Bit1(in_2));
  _2BitDecoder u_2bitdecoder_5 (
    .Bit0(in_1), .Enable(n2bitdecoder_1_out_7), .out_4(n2bitdecoder_5_out_4), .out_5(n2bitdecoder_5_out_5),
    .out_6(n2bitdecoder_5_out_6), .out_7(n2bitdecoder_5_out_7), .Bit1(in_2));
endmodule

module Multiplexer (
  input  in_1,
  input  in_2,
  input  in_3,
  output out_4
);

  wire and_1_out, and_2_out;

  and and_1 (and_1_out, in_1, ~in_3);  // AND_Gate
  or or_1 (out_4, and_1_out, and_2_out);
  and and_2 (and_2_out, in_3, in_2);
endmodule

module CascadeMultiplexer (
  input  in_1,
  input  in_2,
  input  in_3,
  input  in_4,
  input  in_5,
  input  in_6,
  output out_7
);

  wire multiplexer_1_out, multiplexer_2_out;

  Multiplexer_part multiplexer_1 (.in0(in_1), .in1(in_2), .out(multiplexer_1_out), .sel(in_5));  // open: en
  Multiplexer_part multiplexer_2 (.in0(in_3), .in1(in_4), .out(multiplexer_2_out), .sel(in_5));  // open: en
  Multiplexer_part multiplexer_3 (
    .in0(multiplexer_1_out), .in1(multiplexer_2_out), .out(out_7), .sel(in_6));  // open: en
endmodule

module CounterDLatch (
  input  in_1,
  input  in_2,
  input  in_3,
  input  in_4,
  output out_5,
  output out_6
);

  wire multiplexer_1_out;

  Multiplexer_part #(.enable("false")) multiplexer_1 (.in0(in_1), .in1(out_6), .out(multiplexer_1_out), .sel(in_2));
  D_Flip_Flop d_ff_1 (.clk(in_3), .D(multiplexer_1_out), .Q(out_5), .Qn(out_6), .en(in_4));  // open: preset, reset
endmodule

module FullCounter (
  input  in_1,
  input  clk,
  input  enable,
  input  Data
);

  wire and_1_out, and_2_out, and_3_out, counterdlatch_1_out_5, counterdlatch_2_out_5, counterdlatch_3_out_5,
       counterdlatch_4_out_5;

  CounterDLatch counterdlatch_1 (
    .in_1(Data), .in_2(in_1), .in_3(clk), .in_4(enable), .out_5(counterdlatch_1_out_5));  // open: out_6
  and and_1 (and_1_out, in_1, counterdlatch_1_out_5);
  CounterDLatch counterdlatch_2 (
    .in_1(Data), .in_2(and_1_out), .in_3(clk), .in_4(enable), .out_5(counterdlatch_2_out_5));  // open: out_6
  and and_2 (and_2_out, in_1, and_1_out, counterdlatch_2_out_5);
  CounterDLatch counterdlatch_3 (
    .in_1(Data), .in_2(and_2_out), .in_3(clk), .in_4(enable), .out_5(counterdlatch_3_out_5));  // open: out_6
  and and_3 (and_3_out, in_1, and_1_out, counterdlatch_3_out_5, counterdlatch_2_out_5);
  CounterDLatch counterdlatch_4 (
    .in_1(Data), .in_2(and_3_out), .in_3(clk), .in_4(enable), .out_5(counterdlatch_4_out_5));  // open: out_6

  // Notes on the sheet:
  //   Partially working but used to get the idea of how it performs
endmodule
