// Logisim project TARD09MIPS.circ as structural Verilog: 10 circuits, main circuit TG00MIPS
module TG00MIPS (
);

  wire clock_1_out, mips_1_halt, stopclk_1_clkout;

  Clock #(.highDuration(8), .lowDuration(8)) clock_1 (.out(clock_1_out));
  StopClk stopclk_1 (.halt(mips_1_halt), .clkin(clock_1_out), .clkout(stopclk_1_clkout));
  MIPS mips_1 (.clk(stopclk_1_clkout), .reset(1'b0), .halt(mips_1_halt));
endmodule

// clk
module MIPS (
  input  clk,
  input  reset,
  output halt
);

  wire EX, FB, FC, FDC, FPC0, FPC1, GTZ, JMP, JMP1, LEZ, RM, WM, WR, Z;
  wire [3:0] alucontrol_1_out, OPALU;
  wire [4:0] instdecoder_1_ib15_11, instdecoder_1_ib20_16, instdecoder_1_ib25_21, multiplexer_4_out,
       multiplexer_6_out;
  wire [5:0] IB50, IB3126;
  wire [15:0] instdecoder_1_ib15_0;
  wire [25:0] bit_extender_1_out, instdecoder_1_ib25_0;
  wire [27:2] multiplexer_3_out;
  wire [31:0] adder_2_out, alu_1_result, bit_extender_2_out, bit_extender_3_out, data_memory_32_1_read_data,
       instruction_memory_1_instruction, multiplexer_1_out, multiplexer_2_out, multiplexer_5_out,
       multiplexer_7_out, multiplexer_8_out, multiplexer_10_out, PC, PC_q, RA, register_file_1_read_data_1,
       register_file_1_read_data_2, shifter_1_out, shifter_2_out;

  // Probe on multiplexer_1_out
  Multiplexer #(.width(32), .enable("false")) multiplexer_1 (
    .in0(adder_2_out), .in1(multiplexer_2_out), .out(multiplexer_1_out), .sel(FPC1));
  Multiplexer #(.width(32), .enable("false")) multiplexer_2 (
    .in0({PC[31:28], multiplexer_3_out, 2'b00}), .in1(PC), .out(multiplexer_2_out), .sel(FPC0));
  Register #(.width(32)) u_PC (.D(multiplexer_1_out), .Q(PC_q), .clk(clk), .clr(reset));  // open: en
  Adder #(.width(32)) adder_1 (.a(32'h4), .b(PC_q), .out(PC));  // open: cin, cout
  // Probe on instruction_memory_1_instruction
  Instruction_memory instruction_memory_1 (.Read_address(PC_q), .Instruction(instruction_memory_1_instruction));
  Multiplexer #(.width(26), .enable("false")) multiplexer_3 (
    .in0(instdecoder_1_ib25_0), .in1(bit_extender_1_out), .out(multiplexer_3_out), .sel(JMP1));
  Bit_Extender #(.in_width(32), .out_width(26), .\type ("sign")) bit_extender_1 (.in(RA), .out(bit_extender_1_out));
  InstDecoder instdecoder_1 (
    .IB(instruction_memory_1_instruction), .IB31_26(IB3126), .IB25_21(instdecoder_1_ib25_21),
    .IB20_16(instdecoder_1_ib20_16), .IB15_11(instdecoder_1_ib15_11), .IB5_0(IB50),
    .IB15_0(instdecoder_1_ib15_0), .IB25_0(instdecoder_1_ib25_0));
  Multiplexer #(.width(5), .enable("false")) multiplexer_4 (
    .in0(instdecoder_1_ib20_16), .in1({5{1'b1}}), .out(multiplexer_4_out), .sel(JMP));
  Multiplexer #(.width(32), .enable("false")) multiplexer_5 (
    .in0(alu_1_result), .in1(PC), .out(multiplexer_5_out), .sel(JMP));
  Multiplexer #(.width(5), .enable("false")) multiplexer_6 (
    .in0(multiplexer_4_out), .in1(instdecoder_1_ib15_11), .out(multiplexer_6_out), .sel(FDC));
  Multiplexer #(.width(32), .enable("false")) multiplexer_7 (
    .in0(data_memory_32_1_read_data), .in1(multiplexer_5_out), .out(multiplexer_7_out), .sel(FC));
  assign bit_extender_2_out = {{16{1'b0}}, instdecoder_1_ib15_0};  // Bit_Extender bit_extender_2
  assign bit_extender_3_out = {{16{instdecoder_1_ib15_0[15]}}, instdecoder_1_ib15_0};  // Bit_Extender bit_extender_3
  Shifter #(.width(32)) shifter_1 (.in(bit_extender_2_out), .\dist (5'b10000), .out(shifter_1_out));
  Register_file register_file_1 (
    .Read_Register_1(instdecoder_1_ib25_21), .Read_Register_2(instdecoder_1_ib20_16),
    .Write_Register(multiplexer_6_out), .Write_Data(multiplexer_7_out),
    .Read_Data_1(register_file_1_read_data_1), .Read_Data_2(register_file_1_read_data_2), .clk(clk),
    .reset(reset), .Write(WR));
  Multiplexer #(.width(32), .enable("false")) multiplexer_8 (
    .in0(bit_extender_3_out), .in1(shifter_1_out), .out(multiplexer_8_out), .sel(EX));
  Shifter #(.width(32)) shifter_2 (.in(multiplexer_8_out), .\dist (5'b00010), .out(shifter_2_out));
  Adder #(.width(32)) adder_2 (.a(PC), .b(shifter_2_out), .out(adder_2_out));  // open: cin, cout
  Multiplexer #(.width(32), .enable("false")) multiplexer_9 (
    .in0(register_file_1_read_data_1), .in1({32{1'b0}}), .out(RA), .sel(EX));
  Multiplexer #(.width(32), .enable("false")) multiplexer_10 (
    .in0(register_file_1_read_data_2), .in1(multiplexer_8_out), .out(multiplexer_10_out), .sel(FB));
  AluControl alucontrol_1 (.IB50(IB50), .OPALU(OPALU), .OUT(alucontrol_1_out));
  ALU alu_1 (
    .A(RA), .B(multiplexer_10_out), .Z(Z), .Result(alu_1_result), .Operation(alucontrol_1_out), .GTZ(GTZ),
    .LEZ(LEZ));
  Unidad_Control unidad_control_1 (
    .IB31_26(IB3126), .Z(Z), .GTZ(GTZ), .LEZ(LEZ), .FPC1(FPC1), .FPC0(FPC0), .JMP(JMP), .FC(FC), .EX(EX),
    .RM(RM), .WM(WM), .OPALU(OPALU), .HALT(halt), .WR(WR), .FB(FB), .FDC(FDC), .JMP1(JMP1));
  Data_Memory_32 data_memory_32_1 (
    .Address(alu_1_result), .Write_Data(register_file_1_read_data_2), .Read_Data(data_memory_32_1_read_data),
    .Write(WM), .clk(clk), .reset(reset), .Read(RM));
endmodule

module Register_file (
  input  clk,
  input  reset,
  input  [4:0] Read_Register_1,
  input  [4:0] Read_Register_2,
  input  [4:0] Write_Register,
  input  [31:0] Write_Data,
  input  Write,
  output [31:0] Read_Data_1,
  output [31:0] Read_Data_2
);

  wire decoder_1_out1, decoder_1_out2, decoder_1_out3, decoder_1_out4, decoder_1_out5, decoder_1_out6,
       decoder_1_out7, decoder_1_out8, decoder_1_out9, decoder_1_out10, decoder_1_out11, decoder_1_out12,
       decoder_1_out13, decoder_1_out14, decoder_1_out15, decoder_1_out16, decoder_1_out17, decoder_1_out18,
       decoder_1_out19, decoder_1_out20, decoder_1_out21, decoder_1_out22, decoder_1_out23, decoder_1_out24,
       decoder_1_out25, decoder_1_out26, decoder_1_out27, decoder_1_out28, decoder_1_out29, decoder_1_out30,
       decoder_1_out31;
  wire [31:0] delayer1x32_1_out, multiplexer_1_out, multiplexer_2_out, R1_q, R2_q, R3_q, R4_q, R5_q, R6_q,
       R7_q, R8_q, R9_q, R10_q, R11_q, R12_q, R13_q, R14_q, R15_q, R16_q, R17_q, R18_q, R19_q, R20_q, R21_q,
       R22_q, R23_q, R24_q, R25_q, R26_q, R27_q, R28_q, R29_q, R30_q, R31_q;

  Decoder #(.select(5), .disabled(0)) decoder_1 (
    .out1(decoder_1_out1), .out2(decoder_1_out2), .out3(decoder_1_out3), .out4(decoder_1_out4),
    .out5(decoder_1_out5), .out6(decoder_1_out6), .out7(decoder_1_out7), .out8(decoder_1_out8),
    .out9(decoder_1_out9), .out10(decoder_1_out10), .out11(decoder_1_out11), .out12(decoder_1_out12),
    .out13(decoder_1_out13), .out14(decoder_1_out14), .out15(decoder_1_out15), .out16(decoder_1_out16),
    .out17(decoder_1_out17), .out18(decoder_1_out18), .out19(decoder_1_out19), .out20(decoder_1_out20),
    .out21(decoder_1_out21), .out22(decoder_1_out22), .out23(decoder_1_out23), .out24(decoder_1_out24),
    .out25(decoder_1_out25), .out26(decoder_1_out26), .out27(decoder_1_out27), .out28(decoder_1_out28),
    .out29(decoder_1_out29), .out30(decoder_1_out30), .out31(decoder_1_out31), .sel(Write_Register),
    .en(Write));  // open: out0
  Delayer1x32 delayer1x32_1 (.in(Write_Data), .out(delayer1x32_1_out));
  Register #(.width(32)) R1 (.D(delayer1x32_1_out), .en(decoder_1_out1), .Q(R1_q), .clk(clk), .clr(reset));
  Register #(.width(32)) R2 (.D(delayer1x32_1_out), .en(decoder_1_out2), .Q(R2_q), .clk(clk), .clr(reset));
  Register #(.width(32)) R3 (.D(delayer1x32_1_out), .en(decoder_1_out3), .Q(R3_q), .clk(clk), .clr(reset));
  Register #(.width(32)) R4 (.D(delayer1x32_1_out), .en(decoder_1_out4), .Q(R4_q), .clk(clk), .clr(reset));
  Register #(.width(32)) R5 (.D(delayer1x32_1_out), .en(decoder_1_out5), .Q(R5_q), .clk(clk), .clr(reset));
  Register #(.width(32)) R6 (.D(delayer1x32_1_out), .en(decoder_1_out6), .Q(R6_q), .clk(clk), .clr(reset));
  Register #(.width(32)) R7 (.D(delayer1x32_1_out), .en(decoder_1_out7), .Q(R7_q), .clk(clk), .clr(reset));
  Register #(.width(32)) R8 (.D(delayer1x32_1_out), .en(decoder_1_out8), .Q(R8_q), .clk(clk), .clr(reset));
  Register #(.width(32)) R9 (.D(delayer1x32_1_out), .en(decoder_1_out9), .Q(R9_q), .clk(clk), .clr(reset));
  Register #(.width(32)) R10 (.D(delayer1x32_1_out), .en(decoder_1_out10), .Q(R10_q), .clk(clk), .clr(reset));
  Register #(.width(32)) R11 (.D(delayer1x32_1_out), .en(decoder_1_out11), .Q(R11_q), .clk(clk), .clr(reset));
  Register #(.width(32)) R12 (.D(delayer1x32_1_out), .en(decoder_1_out12), .Q(R12_q), .clk(clk), .clr(reset));
  Register #(.width(32)) R13 (.D(delayer1x32_1_out), .en(decoder_1_out13), .Q(R13_q), .clk(clk), .clr(reset));
  Register #(.width(32)) R14 (.D(delayer1x32_1_out), .en(decoder_1_out14), .Q(R14_q), .clk(clk), .clr(reset));
  Register #(.width(32)) R15 (.D(delayer1x32_1_out), .en(decoder_1_out15), .Q(R15_q), .clk(clk), .clr(reset));
  Register #(.width(32)) R16 (.D(delayer1x32_1_out), .en(decoder_1_out16), .Q(R16_q), .clk(clk), .clr(reset));
  Register #(.width(32)) R17 (.D(delayer1x32_1_out), .en(decoder_1_out17), .Q(R17_q), .clk(clk), .clr(reset));
  Register #(.width(32)) R18 (.D(delayer1x32_1_out), .en(decoder_1_out18), .Q(R18_q), .clk(clk), .clr(reset));
  Register #(.width(32)) R19 (.D(delayer1x32_1_out), .en(decoder_1_out19), .Q(R19_q), .clk(clk), .clr(reset));
  Register #(.width(32)) R20 (.D(delayer1x32_1_out), .en(decoder_1_out20), .Q(R20_q), .clk(clk), .clr(reset));
  Register #(.width(32)) R21 (.D(delayer1x32_1_out), .en(decoder_1_out21), .Q(R21_q), .clk(clk), .clr(reset));
  Register #(.width(32)) R22 (.D(delayer1x32_1_out), .en(decoder_1_out22), .Q(R22_q), .clk(clk), .clr(reset));
  Register #(.width(32)) R23 (.D(delayer1x32_1_out), .en(decoder_1_out23), .Q(R23_q), .clk(clk), .clr(reset));
  Register #(.width(32)) R24 (.D(delayer1x32_1_out), .en(decoder_1_out24), .Q(R24_q), .clk(clk), .clr(reset));
  Register #(.width(32)) R25 (.D(delayer1x32_1_out), .en(decoder_1_out25), .Q(R25_q), .clk(clk), .clr(reset));
  Register #(.width(32)) R26 (.D(delayer1x32_1_out), .en(decoder_1_out26), .Q(R26_q), .clk(clk), .clr(reset));
  Register #(.width(32)) R27 (.D(delayer1x32_1_out), .en(decoder_1_out27), .Q(R27_q), .clk(clk), .clr(reset));
  Register #(.width(32)) R28 (.D(delayer1x32_1_out), .en(decoder_1_out28), .Q(R28_q), .clk(clk), .clr(reset));
  Register #(.width(32)) R29 (.D(delayer1x32_1_out), .en(decoder_1_out29), .Q(R29_q), .clk(clk), .clr(reset));
  Register #(.width(32)) R30 (.D(delayer1x32_1_out), .en(decoder_1_out30), .Q(R30_q), .clk(clk), .clr(reset));
  Register #(.width(32)) R31 (.D(delayer1x32_1_out), .en(decoder_1_out31), .Q(R31_q), .clk(clk), .clr(reset));
  Multiplexer #(.select(5), .width(32), .enable("false")) multiplexer_1 (
    .in0({32{1'b0}}), .in1(R1_q), .in2(R2_q), .in3(R3_q), .in4(R4_q), .in5(R5_q), .in6(R6_q), .in7(R7_q),
    .in8(R8_q), .in9(R9_q), .in10(R10_q), .in11(R11_q), .in12(R12_q), .in13(R13_q), .in14(R14_q),
    .in15(R15_q), .in16(R16_q), .in17(R17_q), .in18(R18_q), .in19(R19_q), .in20(R20_q), .in21(R21_q),
    .in22(R22_q), .in23(R23_q), .in24(R24_q), .in25(R25_q), .in26(R26_q), .in27(R27_q), .in28(R28_q),
    .in29(R29_q), .in30(R30_q), .in31(R31_q), .out(multiplexer_1_out), .sel(Read_Register_1));
  Multiplexer #(.select(5), .width(32), .enable("false")) multiplexer_2 (
    .in0({32{1'b0}}), .in1(R1_q), .in2(R2_q), .in3(R3_q), .in4(R4_q), .in5(R5_q), .in6(R6_q), .in7(R7_q),
    .in8(R8_q), .in9(R9_q), .in10(R10_q), .in11(R11_q), .in12(R12_q), .in13(R13_q), .in14(R14_q),
    .in15(R15_q), .in16(R16_q), .in17(R17_q), .in18(R18_q), .in19(R19_q), .in20(R20_q), .in21(R21_q),
    .in22(R22_q), .in23(R23_q), .in24(R24_q), .in25(R25_q), .in26(R26_q), .in27(R27_q), .in28(R28_q),
    .in29(R29_q), .in30(R30_q), .in31(R31_q), .out(multiplexer_2_out), .sel(Read_Register_2));
  Delayer1x32 delayer1x32_2 (.in(multiplexer_1_out), .out(Read_Data_1));
  Delayer1x32 delayer1x32_3 (.in(multiplexer_2_out), .out(Read_Data_2));
endmodule

module ALU (
  input  [3:0] Operation,
  input  [31:0] A,
  input  [31:0] B,
  output Z,
  output [31:0] Result,
  output GTZ,
  output LEZ
);

  wire comparator_1_eq, nor_1_out;
  wire [0:0] comparator_1_lt;
  wire [31:0] adder_1_out, and_1_out, multiplexer_1_out, multiplexer_2_out, multiplexer_3_out, not_1_out,
       not_2_out, or_2_out;

  assign not_1_out = ~A;  // NOT_Gate not_1, 32 bits wide
  assign not_2_out = ~B;  // NOT_Gate not_2, 32 bits wide
  Comparator #(.width(32)) comparator_1 (.a(A), .b(B), .gt(GTZ), .eq(comparator_1_eq), .lt(comparator_1_lt[0]));
  Multiplexer #(.width(32), .enable("false")) multiplexer_1 (
    .in0(A), .in1(not_1_out), .out(multiplexer_1_out), .sel(Operation[3]));
  Multiplexer #(.width(32), .enable("false")) multiplexer_2 (
    .in0(B), .in1(not_2_out), .out(multiplexer_2_out), .sel(Operation[2]));
  or or_1 (LEZ, comparator_1_eq, comparator_1_lt[0]);
  assign and_1_out = multiplexer_1_out & multiplexer_2_out;  // AND_Gate and_1, 32 bits wide
  assign or_2_out = multiplexer_1_out | multiplexer_2_out;  // OR_Gate or_2, 32 bits wide
  Adder #(.width(32)) adder_1 (
    .a(multiplexer_1_out), .b(multiplexer_2_out), .out(adder_1_out), .cin(Operation[2]));  // open: cout
  Multiplexer #(.select(2), .width(32), .enable("false")) multiplexer_3 (
    .in0(and_1_out), .in1(or_2_out), .in2(adder_1_out), .in3({{31{1'b0}}, comparator_1_lt[0]}),
    .out(multiplexer_3_out), .sel(Operation[1:0]));
  nor nor_1 (nor_1_out, multiplexer_3_out[0], multiplexer_3_out[1], multiplexer_3_out[2], multiplexer_3_out[3], multiplexer_3_out[4], multiplexer_3_out[5], multiplexer_3_out[6], multiplexer_3_out[7], multiplexer_3_out[8], multiplexer_3_out[9], multiplexer_3_out[10], multiplexer_3_out[11], multiplexer_3_out[12], multiplexer_3_out[13], multiplexer_3_out[14], multiplexer_3_out[15], multiplexer_3_out[16], multiplexer_3_out[17], multiplexer_3_out[18], multiplexer_3_out[19], multiplexer_3_out[20], multiplexer_3_out[21], multiplexer_3_out[22], multiplexer_3_out[23], multiplexer_3_out[24], multiplexer_3_out[25], multiplexer_3_out[26], multiplexer_3_out[27], multiplexer_3_out[28], multiplexer_3_out[29], multiplexer_3_out[30], multiplexer_3_out[31]);
  Delayer2x32 delayer2x32_1 (.in(multiplexer_3_out), .out(Result));
  Delayer2x1 delayer2x1_1 (.in(nor_1_out), .out(Z));

  // Notes on the sheet:
  //   0001    OR
  //   Operation    Function
  //   0000    AND
  //   0010    add
  //   0110    subtract
  //   0111    set on less than
  //   1100    NOR
endmodule

module Data_Memory_32 (
  input  Write,
  input  [31:0] Address,
  input  [31:0] Write_Data,
  input  clk,
  input  reset,
  input  Read,
  output [31:0] Read_Data
);

  wire [9:0] bitselector_1_out;
  wire [31:0] delayer2x32_1_out, ram_1_data;

  BitSelector #(.width(32), .group(10)) bitselector_1 (.in(Address), .out(bitselector_1_out), .sel(2'b00));
  Delayer2x32 delayer2x32_1 (.in(Write_Data), .out(delayer2x32_1_out));
  RAM #(.dataWidth(32), .bus("separate")) ram_1 (
    .addr(bitselector_1_out[9:2]), .din(delayer2x32_1_out), .data(ram_1_data), .str(Write), .sel(1'b1),
    .clk(clk), .ld(Read), .clr(reset));
  Delayer2x32 delayer2x32_2 (.in(ram_1_data), .out(Read_Data));

  // Notes on the sheet:
  //   Memoria de 32 bits direccionable a nivel de byte
  //   Tan solo implementadas las 256 primeras posiciones de 32 bits o 1024 bytes
endmodule

module Instruction_memory (
  input  [31:0] Read_address,
  output [31:0] Instruction
);

  wire [6:0] bitselector_1_out;
  wire [31:0] ram_1_data;

  BitSelector #(.width(30), .group(7)) bitselector_1 (.in(Read_address[31:2]), .out(bitselector_1_out), .sel(3'b000));
  RAM #(.addrWidth(7), .dataWidth(32), .bus("asynch"), .Datafile_on_reset("TG00rom.txt")) ram_1 (
    .addr(bitselector_1_out), .data(ram_1_data), .sel(1'b1), .ld(1'b1), .clr(1'b0));
  Delayer2x32 delayer2x32_1 (.in(ram_1_data), .out(Instruction));
endmodule

module InstDecoder (
  input  [31:0] IB,
  output [5:0] IB31_26,
  output [4:0] IB25_21,
  output [4:0] IB20_16,
  output [4:0] IB15_11,
  output [5:0] IB5_0,
  output [15:0] IB15_0,
  output [25:0] IB25_0
);


  assign IB5_0 = IB[5:0];
  assign IB15_0 = IB[15:0];
  assign IB15_11 = IB[15:11];
  assign IB20_16 = IB[20:16];
  assign IB25_0 = IB[25:0];
  assign IB25_21 = IB[25:21];
  assign IB31_26 = IB[31:26];
endmodule

module AluControl (
  input  [5:0] IB50,
  input  [3:0] OPALU,
  output [3:0] OUT
);

  wire and_1_out, not_1_out;
  wire [3:0] rom_1_data;

  and and_1 (and_1_out, OPALU[0], OPALU[1], OPALU[2], OPALU[3]);
  ROM #(.addrWidth(6), .dataWidth(4)) rom_1 (.addr(IB50), .data(rom_1_data));  // open: sel
  Multiplexer #(.width(4), .enable("false")) multiplexer_1 (.in0(rom_1_data), .in1(OPALU), .out(OUT), .sel(not_1_out));
  not not_1 (not_1_out, and_1_out);

  // Notes on the sheet:
  //   contents of rom_1 (hex, n*v repeats v):
  //   32*0 2 0 6 0 0 1 4*0 7
endmodule

module Unidad_Control (
  input  [5:0] IB31_26,
  input  Z,
  input  GTZ,
  input  LEZ,
  output FPC1,
  output FPC0,
  output JMP,
  output FC,
  output EX,
  output RM,
  output WM,
  output [3:0] OPALU,
  output HALT,
  output WR,
  output FB,
  output FDC,
  output JMP1
);

  wire ADI_out, ANDI_out, BE_out, BEQ_out, BGTZ_2_out, BGTZ_3_out, BGTZ_out, BLEZ_out, BNE_2_out, BNE_out,
       JMP_out, LW_out, not_1_out, OPALU_out, or_1_out, or_2_out, or_3_out, ORI_out, SW_out;

  and u_OPALU (OPALU_out, ~IB31_26[0], ~IB31_26[1], ~IB31_26[2], ~IB31_26[3], ~IB31_26[4], ~IB31_26[5]);  // AND_Gate
  and SW (SW_out, IB31_26[0], IB31_26[1], ~IB31_26[2], IB31_26[3], ~IB31_26[4], IB31_26[5]);  // AND_Gate
  and JR (JMP1, ~IB31_26[0], ~IB31_26[1], ~IB31_26[2], ~IB31_26[3], ~IB31_26[4], IB31_26[5]);  // AND_Gate
  and JAL (JMP, IB31_26[0], IB31_26[1], ~IB31_26[2], ~IB31_26[3], ~IB31_26[4], ~IB31_26[5]);  // AND_Gate
  and u_JMP (JMP_out, ~IB31_26[0], IB31_26[1], ~IB31_26[2], ~IB31_26[3], ~IB31_26[4], ~IB31_26[5]);  // AND_Gate
  and u_HALT (HALT, IB31_26[0], IB31_26[1], IB31_26[2], IB31_26[3], IB31_26[4], IB31_26[5]);
  and ADI (ADI_out, ~IB31_26[0], ~IB31_26[1], ~IB31_26[2], IB31_26[3], ~IB31_26[4], ~IB31_26[5]);  // AND_Gate
  and ANDI (ANDI_out, ~IB31_26[0], ~IB31_26[1], IB31_26[2], IB31_26[3], ~IB31_26[4], ~IB31_26[5]);  // AND_Gate
  and ORI (ORI_out, IB31_26[0], ~IB31_26[1], IB31_26[2], IB31_26[3], ~IB31_26[4], ~IB31_26[5]);  // AND_Gate
  and LUI (EX, IB31_26[0], IB31_26[1], IB31_26[2], IB31_26[3], ~IB31_26[4], ~IB31_26[5]);  // AND_Gate
  and LW (LW_out, IB31_26[0], IB31_26[1], ~IB31_26[2], ~IB31_26[3], ~IB31_26[4], IB31_26[5]);  // AND_Gate
  and BLEZ (BLEZ_out, ~IB31_26[0], IB31_26[1], IB31_26[2], ~IB31_26[3], ~IB31_26[4], ~IB31_26[5]);  // AND_Gate
  and BGTZ (BGTZ_out, IB31_26[0], IB31_26[1], IB31_26[2], ~IB31_26[3], ~IB31_26[4], ~IB31_26[5]);  // AND_Gate
  and BNE (BNE_out, IB31_26[0], ~IB31_26[1], IB31_26[2], ~IB31_26[3], ~IB31_26[4], ~IB31_26[5]);  // AND_Gate
  and BEQ (BEQ_out, ~IB31_26[0], ~IB31_26[1], IB31_26[2], ~IB31_26[3], ~IB31_26[4], ~IB31_26[5]);  // AND_Gate
  or or_1 (or_1_out, JMP, JMP1, JMP_out);
  or or_2 (or_2_out, BLEZ_out, BNE_out, BGTZ_out, BEQ_out);
  not not_1 (not_1_out, Z);
  and BE (BE_out, BEQ_out, Z);
  TablaOP tablaop_1 (
    .ANDI(ANDI_out), .JUMP(or_1_out), .ADDI(ADI_out), .OPALU(OPALU_out), .LW(LW_out), .BEQ(or_2_out),
    .SW(SW_out), .FPC0(FPC0), .FC(FC), .RM(RM), .WM(WM), .OPALU0(OPALU[3]), .OPALU1(OPALU[2]),
    .OPALU2(OPALU[1]), .OPALU3(OPALU[0]), .WR(WR), .FB(FB), .FDC(FDC), .ORI(ORI_out), .LUI(EX));
  and BGTZ_2 (BGTZ_2_out, BLEZ_out, LEZ);
  and BGTZ_3 (BGTZ_3_out, BGTZ_out, GTZ);
  and BNE_2 (BNE_2_out, not_1_out, BNE_out);
  or or_3 (or_3_out, BNE_2_out, BGTZ_2_out, BGTZ_3_out, BE_out);
  not not_2 (FPC1, or_3_out);
endmodule

module TablaOP (
  input  ANDI,
  input  JUMP,
  input  ADDI,
  input  OPALU,
  input  LW,
  input  BEQ,
  input  SW,
  input  ORI,
  input  LUI,
  output FPC0,
  output FC,
  output RM,
  output WM,
  output OPALU0,
  output OPALU1,
  output OPALU2,
  output OPALU3,
  output WR,
  output FB,
  output FDC
);

  wire not_3_out, not_4_out, not_5_out, not_6_out, not_7_out, not_8_out, not_9_out, not_10_out, not_11_out,
       not_12_out;

  not not_1 (FC, LW);
  not not_2 (RM, SW);
  not not_3 (not_3_out, ADDI);
  not not_4 (not_4_out, LW);
  not not_5 (not_5_out, ORI);
  not not_6 (not_6_out, SW);
  not not_7 (not_7_out, ANDI);
  not not_8 (not_8_out, LUI);
  not not_9 (not_9_out, ANDI);
  not not_10 (not_10_out, ORI);
  not not_11 (not_11_out, OPALU);
  and and_1 (FB, not_11_out, not_12_out);
  not not_12 (not_12_out, BEQ);
  or or_1 (FPC0, ANDI, OPALU, ORI, LUI, SW, BEQ, LW, ADDI);
  and and_2 (OPALU1, not_3_out, not_4_out, not_5_out, not_6_out, not_7_out, not_8_out);
  and and_3 (OPALU2, not_9_out, not_10_out);
  or or_2 (OPALU3, OPALU, ORI);
  or or_3 (WR, ANDI, JUMP, ADDI, LW, ORI, BEQ, SW, OPALU, LUI);

  assign FDC = OPALU;
  assign OPALU0 = OPALU;
  assign WM = SW;

  // Notes on the sheet:
  //   ALU
  //   Operation    Function
  //   0000    AND
  //   0001    OR
  //   0010    add
  //   0110    subtract
  //   0111    set on less than
  //   1100    NOR
endmodule
