// Logisim project Finished.circ as structural Verilog: 10 circuits, main circuit TG00MIPS
module TG00MIPS (
);

  wire clock_1_out, mips_1_halt, stopclk_1_clkout;

  Clock #(.highDuration(2), .lowDuration(2)) clock_1 (.out(clock_1_out));
  StopClk stopclk_1 (.halt(mips_1_halt), .clkin(clock_1_out), .clkout(stopclk_1_clkout));
  MIPS mips_1 (.clk(stopclk_1_clkout), .reset(1'b0), .halt(mips_1_halt));
endmodule

// clk
module MIPS (
  input  clk,
  input  reset,
  output halt
);

  wire ALU0, ALU1, ALUSrc, MemRead, MemToReg, MemWrte, not_1_out, opcode_simple_1_jmp_2, or_1_out, RegDst,
       RegWrte;
  wire [3:0] alucontrol_1_out;
  wire [4:0] multiplexer_1_out, opcode_simple_1_rd, opcode_simple_1_rf1, opcode_simple_1_rf2;
  wire [5:0] opcode_simple_1_opalu;
  wire [6:0] ttycntrl_1_out;
  wire [15:0] opcode_simple_1_out;
  wire [31:0] adder_1_out, alu_1_result, controlled_buffer_1_out, data_memory_32_1_read_data,
       instruction_memory_1_instruction, multiplexer_3_out, opcode_simple_1_jmp, OUT16, PC,
       register_file_1_read_data_1, register_file_1_read_data_2, undriven;

  assign controlled_buffer_1_out = or_1_out ? opcode_simple_1_jmp : 32'bz;  // Controlled_Buffer controlled_buffer_1
  Register #(.width(32)) u_PC (.D(controlled_buffer_1_out), .Q(PC), .clk(clk), .clr(reset));  // open: en
  Adder #(.width(32)) adder_1 (.a(32'h4), .b(PC), .out(adder_1_out));  // open: cin, cout
  TTY #(.rows(10), .cols(44)) tty_1 (.data(ttycntrl_1_out), .clk(clk));  // open: we, clr
  TTYCntrl ttycntrl_1 (.in_1(clk), .OUT(ttycntrl_1_out));
  Instruction_memory instruction_memory_1 (.Read_address(PC), .Instruction(instruction_memory_1_instruction));
  assign controlled_buffer_1_out = not_1_out ? adder_1_out : 32'bz;  // Controlled_Buffer controlled_buffer_2
  not not_1 (not_1_out, or_1_out);
  OPCODE_SIMPLE opcode_simple_1 (
    .in_2(instruction_memory_1_instruction), .OUT(opcode_simple_1_out), .JMP_2(opcode_simple_1_jmp_2),
    .BEQ(ALU1), .OPALU_2(ALU0), .HALT(halt), .PC(PC), .RD(opcode_simple_1_rd), .RF1(opcode_simple_1_rf1),
    .OPALU(opcode_simple_1_opalu), .RegDst(RegDst), .RegWrte(RegWrte), .ALUSrc(ALUSrc),
    .RF2(opcode_simple_1_rf2), .JMP(opcode_simple_1_jmp), .MemWrte(MemWrte), .MemRead(MemRead),
    .MemToReg(MemToReg));  // open: ADDI, LW, SW
  assign OUT16 = {{16{opcode_simple_1_out[15]}}, opcode_simple_1_out};  // Bit_Extender bit_extender_1
  or or_1 (or_1_out, opcode_simple_1_jmp_2, ALU1);
  Multiplexer #(.width(5), .enable("false")) multiplexer_1 (
    .in0(opcode_simple_1_rd), .in1(opcode_simple_1_rf2), .out(multiplexer_1_out), .sel(RegDst));
  Register_file register_file_1 (
    .Read_Register_1(opcode_simple_1_rf1), .Read_Register_2(opcode_simple_1_rd),
    .Write_Register(multiplexer_1_out), .Write_Data(multiplexer_3_out),
    .Read_Data_1(register_file_1_read_data_1), .Read_Data_2(register_file_1_read_data_2), .clk(clk),
    .reset(reset), .Write(RegWrte));
  AluControl alucontrol_1 (.alop0(ALU0), .alop1(ALU1), .in_3(opcode_simple_1_opalu), .OUT(alucontrol_1_out));
  Multiplexer #(.width(32), .enable("false")) multiplexer_2 (
    .in0(register_file_1_read_data_2), .in1(OUT16), .sel(ALUSrc));  // open: out
  ALU alu_1 (
    .A(register_file_1_read_data_1), .B(undriven), .Result(alu_1_result), .Operation(alucontrol_1_out));  // open: Z
  Data_Memory_32 data_memory_32_1 (
    .Address(alu_1_result), .Write_Data(register_file_1_read_data_2), .Read_Data(data_memory_32_1_read_data),
    .Write(MemWrte), .clk(clk), .reset(reset), .Read(MemRead));
  Multiplexer #(.width(32), .enable("false")) multiplexer_3 (
    .in0(data_memory_32_1_read_data), .in1(alu_1_result), .out(multiplexer_3_out), .sel(MemToReg));
endmodule

module Register_file (
  input  clk,
  input  reset,
  input  [4:0] Read_Register_1,
  input  [4:0] Read_Register_2,
  input  [4:0] Write_Register,
  input  [31:0] Write_Data,
  input  Write,
  output [31:0] Read_Data_1,
  output [31:0] Read_Data_2
);

  wire decoder_1_out1, decoder_1_out2, decoder_1_out3, decoder_1_out4, decoder_1_out5, decoder_1_out6,
       decoder_1_out7, decoder_1_out8, decoder_1_out9, decoder_1_out10, decoder_1_out11, decoder_1_out12,
       decoder_1_out13, decoder_1_out14, decoder_1_out15, decoder_1_out16, decoder_1_out17, decoder_1_out18,
       decoder_1_out19, decoder_1_out20, decoder_1_out21, decoder_1_out22, decoder_1_out23, decoder_1_out24,
       decoder_1_out25, decoder_1_out26, decoder_1_out27, decoder_1_out28, decoder_1_out29, decoder_1_out30,
       decoder_1_out31;
  wire [31:0] delayer1x32_1_out, multiplexer_1_out, multiplexer_2_out, R1_q, R2_q, R3_q, R4_q, R5_q, R6_q,
       R7_q, R8_q, R9_q, R10_q, R11_q, R12_q, R13_q, R14_q, R15_q, R16_q, R17_q, R18_q, R19_q, R20_q, R21_q,
       R22_q, R23_q, R24_q, R25_q, R26_q, R27_q, R28_q, R29_q, R30_q, R31_q;

  Decoder #(.select(5), .disabled(0)) decoder_1 (
    .out1(decoder_1_out1), .out2(decoder_1_out2), .out3(decoder_1_out3), .out4(decoder_1_out4),
    .out5(decoder_1_out5), .out6(decoder_1_out6), .out7(decoder_1_out7), .out8(decoder_1_out8),
    .out9(decoder_1_out9), .out10(decoder_1_out10), .out11(decoder_1_out11), .out12(decoder_1_out12),
    .out13(decoder_1_out13), .out14(decoder_1_out14), .out15(decoder_1_out15), .out16(decoder_1_out16),
    .out17(decoder_1_out17), .out18(decoder_1_out18), .out19(decoder_1_out19), .out20(decoder_1_out20),
    .out21(decoder_1_out21), .out22(decoder_1_out22), .out23(decoder_1_out23), .out24(decoder_1_out24),
    .out25(decoder_1_out25), .out26(decoder_1_out26), .out27(decoder_1_out27), .out28(decoder_1_out28),
    .out29(decoder_1_out29), .out30(decoder_1_out30), .out31(decoder_1_out31), .sel(Write_Register),
    .en(Write));  // open: out0
  Delayer1x32 delayer1x32_1 (.in(Write_Data), .out(delayer1x32_1_out));
  Register #(.width(32)) R1 (.D(delayer1x32_1_out), .en(decoder_1_out1), .Q(R1_q), .clk(clk), .clr(reset));
  Register #(.width(32)) R2 (.D(delayer1x32_1_out), .en(decoder_1_out2), .Q(R2_q), .clk(clk), .clr(reset));
  Register #(.width(32)) R3 (.D(delayer1x32_1_out), .en(decoder_1_out3), .Q(R3_q), .clk(clk), .clr(reset));
  Register #(.width(32)) R4 (.D(delayer1x32_1_out), .en(decoder_1_out4), .Q(R4_q), .clk(clk), .clr(reset));
  Register #(.width(32)) R5 (.D(delayer1x32_1_out), .en(decoder_1_out5), .Q(R5_q), .clk(clk), .clr(reset));
  Register #(.width(32)) R6 (.D(delayer1x32_1_out), .en(decoder_1_out6), .Q(R6_q), .clk(clk), .clr(reset));
  Register #(.width(32)) R7 (.D(delayer1x32_1_out), .en(decoder_1_out7), .Q(R7_q), .clk(clk), .clr(reset));
  Register #(.width(32)) R8 (.D(delayer1x32_1_out), .en(decoder_1_out8), .Q(R8_q), .clk(clk), .clr(reset));
  Register #(.width(32)) R9 (.D(delayer1x32_1_out), .en(decoder_1_out9), .Q(R9_q), .clk(clk), .clr(reset));
  Register #(.width(32)) R10 (.D(delayer1x32_1_out), .en(decoder_1_out10), .Q(R10_q), .clk(clk), .clr(reset));
  Register #(.width(32)) R11 (.D(delayer1x32_1_out), .en(decoder_1_out11), .Q(R11_q), .clk(clk), .clr(reset));
  Register #(.width(32)) R12 (.D(delayer1x32_1_out), .en(decoder_1_out12), .Q(R12_q), .clk(clk), .clr(reset));
  Register #(.width(32)) R13 (.D(delayer1x32_1_out), .en(decoder_1_out13), .Q(R13_q), .clk(clk), .clr(reset));
  Register #(.width(32)) R14 (.D(delayer1x32_1_out), .en(decoder_1_out14), .Q(R14_q), .clk(clk), .clr(reset));
  Register #(.width(32)) R15 (.D(delayer1x32_1_out), .en(decoder_1_out15), .Q(R15_q), .clk(clk), .clr(reset));
  Register #(.width(32)) R16 (.D(delayer1x32_1_out), .en(decoder_1_out16), .Q(R16_q), .clk(clk), .clr(reset));
  Register #(.width(32)) R17 (.D(delayer1x32_1_out), .en(decoder_1_out17), .Q(R17_q), .clk(clk), .clr(reset));
  Register #(.width(32)) R18 (.D(delayer1x32_1_out), .en(decoder_1_out18), .Q(R18_q), .clk(clk), .clr(reset));
  Register #(.width(32)) R19 (.D(delayer1x32_1_out), .en(decoder_1_out19), .Q(R19_q), .clk(clk), .clr(reset));
  Register #(.width(32)) R20 (.D(delayer1x32_1_out), .en(decoder_1_out20), .Q(R20_q), .clk(clk), .clr(reset));
  Register #(.width(32)) R21 (.D(delayer1x32_1_out), .en(decoder_1_out21), .Q(R21_q), .clk(clk), .clr(reset));
  Register #(.width(32)) R22 (.D(delayer1x32_1_out), .en(decoder_1_out22), .Q(R22_q), .clk(clk), .clr(reset));
  Register #(.width(32)) R23 (.D(delayer1x32_1_out), .en(decoder_1_out23), .Q(R23_q), .clk(clk), .clr(reset));
  Register #(.width(32)) R24 (.D(delayer1x32_1_out), .en(decoder_1_out24), .Q(R24_q), .clk(clk), .clr(reset));
  Register #(.width(32)) R25 (.D(delayer1x32_1_out), .en(decoder_1_out25), .Q(R25_q), .clk(clk), .clr(reset));
  Register #(.width(32)) R26 (.D(delayer1x32_1_out), .en(decoder_1_out26), .Q(R26_q), .clk(clk), .clr(reset));
  Register #(.width(32)) R27 (.D(delayer1x32_1_out), .en(decoder_1_out27), .Q(R27_q), .clk(clk), .clr(reset));
  Register #(.width(32)) R28 (.D(delayer1x32_1_out), .en(decoder_1_out28), .Q(R28_q), .clk(clk), .clr(reset));
  Register #(.width(32)) R29 (.D(delayer1x32_1_out), .en(decoder_1_out29), .Q(R29_q), .clk(clk), .clr(reset));
  Register #(.width(32)) R30 (.D(delayer1x32_1_out), .en(decoder_1_out30), .Q(R30_q), .clk(clk), .clr(reset));
  Register #(.width(32)) R31 (.D(delayer1x32_1_out), .en(decoder_1_out31), .Q(R31_q), .clk(clk), .clr(reset));
  Multiplexer #(.select(5), .width(32), .enable("false")) multiplexer_1 (
    .in0({32{1'b0}}), .in1(R1_q), .in2(R2_q), .in3(R3_q), .in4(R4_q), .in5(R5_q), .in6(R6_q), .in7(R7_q),
    .in8(R8_q), .in9(R9_q), .in10(R10_q), .in11(R11_q), .in12(R12_q), .in13(R13_q), .in14(R14_q),
    .in15(R15_q), .in16(R16_q), .in17(R17_q), .in18(R18_q), .in19(R19_q), .in20(R20_q), .in21(R21_q),
    .in22(R22_q), .in23(R23_q), .in24(R24_q), .in25(R25_q), .in26(R26_q), .in27(R27_q), .in28(R28_q),
    .in29(R29_q), .in30(R30_q), .in31(R31_q), .out(multiplexer_1_out), .sel(Read_Register_1));
  Multiplexer #(.select(5), .width(32), .enable("false")) multiplexer_2 (
    .in0({32{1'b0}}), .in1(R1_q), .in2(R2_q), .in3(R3_q), .in4(R4_q), .in5(R5_q), .in6(R6_q), .in7(R7_q),
    .in8(R8_q), .in9(R9_q), .in10(R10_q), .in11(R11_q), .in12(R12_q), .in13(R13_q), .in14(R14_q),
    .in15(R15_q), .in16(R16_q), .in17(R17_q), .in18(R18_q), .in19(R19_q), .in20(R20_q), .in21(R21_q),
    .in22(R22_q), .in23(R23_q), .in24(R24_q), .in25(R25_q), .in26(R26_q), .in27(R27_q), .in28(R28_q),
    .in29(R29_q), .in30(R30_q), .in31(R31_q), .out(multiplexer_2_out), .sel(Read_Register_2));
  Delayer1x32 delayer1x32_2 (.in(multiplexer_1_out), .out(Read_Data_1));
  Delayer1x32 delayer1x32_3 (.in(multiplexer_2_out), .out(Read_Data_2));
endmodule

module ALU (
  input  [3:0] Operation,
  input  [31:0] A,
  input  [31:0] B,
  output Z,
  output [31:0] Result
);

  wire nor_1_out;
  wire [0:0] comparator_1_lt;
  wire [31:0] adder_1_out, and_1_out, multiplexer_1_out, multiplexer_2_out, multiplexer_3_out, not_1_out,
       not_2_out, or_1_out;

  assign not_1_out = ~A;  // NOT_Gate not_1, 32 bits wide
  assign not_2_out = ~B;  // NOT_Gate not_2, 32 bits wide
  Comparator #(.width(32)) comparator_1 (.a(A), .b(B), .lt(comparator_1_lt[0]));  // open: gt, eq
  Multiplexer #(.width(32), .enable("false")) multiplexer_1 (
    .in0(A), .in1(not_1_out), .out(multiplexer_1_out), .sel(Operation[3]));
  Multiplexer #(.width(32), .enable("false")) multiplexer_2 (
    .in0(B), .in1(not_2_out), .out(multiplexer_2_out), .sel(Operation[2]));
  assign and_1_out = multiplexer_1_out & multiplexer_2_out;  // AND_Gate and_1, 32 bits wide
  assign or_1_out = multiplexer_1_out | multiplexer_2_out;  // OR_Gate or_1, 32 bits wide
  Adder #(.width(32)) adder_1 (
    .a(multiplexer_1_out), .b(multiplexer_2_out), .out(adder_1_out), .cin(Operation[2]));  // open: cout
  Multiplexer #(.select(2), .width(32), .enable("false")) multiplexer_3 (
    .in0(and_1_out), .in1(or_1_out), .in2(adder_1_out), .in3({{31{1'b0}}, comparator_1_lt[0]}),
    .out(multiplexer_3_out), .sel(Operation[1:0]));
  nor nor_1 (nor_1_out, multiplexer_3_out[0], multiplexer_3_out[1], multiplexer_3_out[2], multiplexer_3_out[3], multiplexer_3_out[4], multiplexer_3_out[5], multiplexer_3_out[6], multiplexer_3_out[7], multiplexer_3_out[8], multiplexer_3_out[9], multiplexer_3_out[10], multiplexer_3_out[11], multiplexer_3_out[12], multiplexer_3_out[13], multiplexer_3_out[14], multiplexer_3_out[15], multiplexer_3_out[16], multiplexer_3_out[17], multiplexer_3_out[18], multiplexer_3_out[19], multiplexer_3_out[20], multiplexer_3_out[21], multiplexer_3_out[22], multiplexer_3_out[23], multiplexer_3_out[24], multiplexer_3_out[25], multiplexer_3_out[26], multiplexer_3_out[27], multiplexer_3_out[28], multiplexer_3_out[29], multiplexer_3_out[30], multiplexer_3_out[31]);
  Delayer2x32 delayer2x32_1 (.in(multiplexer_3_out), .out(Result));
  Delayer2x1 delayer2x1_1 (.in(nor_1_out), .out(Z));

  // Notes on the sheet:
  //   0001    OR
  //   Operation    Function
  //   0000    AND
  //   0010    add
  //   0110    subtract
  //   0111    set on less than
  //   1100    NOR
endmodule

module Data_Memory_32 (
  input  Write,
  input  [31:0] Address,
  input  [31:0] Write_Data,
  input  clk,
  input  reset,
  input  Read,
  output [31:0] Read_Data
);

  wire [9:0] bitselector_1_out;
  wire [31:0] delayer2x32_1_out, ram_1_data;

  BitSelector #(.width(32), .group(10)) bitselector_1 (.in(Address), .out(bitselector_1_out), .sel(2'b00));
  Delayer2x32 delayer2x32_1 (.in(Write_Data), .out(delayer2x32_1_out));
  RAM #(.dataWidth(32), .bus("separate")) ram_1 (
    .addr(bitselector_1_out[9:2]), .din(delayer2x32_1_out), .data(ram_1_data), .str(Write), .sel(1'b1),
    .clk(clk), .ld(Read), .clr(reset));
  Delayer2x32 delayer2x32_2 (.in(ram_1_data), .out(Read_Data));

  // Notes on the sheet:
  //   Memoria de 32 bits direccionable a nivel de byte
  //   Tan solo implementadas las 256 primeras posiciones de 32 bits o 1024 bytes
endmodule

module Instruction_memory (
  input  [31:0] Read_address,
  output [31:0] Instruction
);

  wire [6:0] bitselector_1_out;
  wire [31:0] ram_1_data;

  BitSelector #(.width(30), .group(7)) bitselector_1 (.in(Read_address[31:2]), .out(bitselector_1_out), .sel(3'b000));
  RAM #(.addrWidth(7), .dataWidth(32), .bus("asynch")) ram_1 (
    .addr(bitselector_1_out), .data(ram_1_data), .sel(1'b1), .ld(1'b1), .clr(1'b0));
  Delayer2x32 delayer2x32_1 (.in(ram_1_data), .out(Instruction));
endmodule

module InstDecoder (
  input  [31:0] IB,
  output [5:0] IB31_26,
  output [4:0] IB25_21,
  output [4:0] IB20_16,
  output [4:0] IB15_11,
  output [5:0] IB5_0,
  output [15:0] IB15_0,
  output [25:0] IB25_0
);


  assign IB5_0 = IB[5:0];
  assign IB15_0 = IB[15:0];
  assign IB15_11 = IB[15:11];
  assign IB20_16 = IB[20:16];
  assign IB25_0 = IB[25:0];
  assign IB25_21 = IB[25:21];
  assign IB31_26 = IB[31:26];
endmodule

module OPCODE_SIMPLE (
  input  [31:0] PC,
  input  [31:0] in_2,
  output [31:0] JMP,
  output [15:0] OUT,
  output [4:0] RD,
  output [4:0] RF1,
  output [4:0] RF2,
  output [5:0] OPALU,
  output RegDst,
  output RegWrte,
  output ALUSrc,
  output MemWrte,
  output MemRead,
  output MemToReg,
  output JMP_2,
  output BEQ,
  output OPALU_2,
  output HALT,
  output ADDI,
  output LW,
  output SW
);

  wire and_1_out, comparator_1_eq, not_1_out, not_2_out, not_3_out, not_4_out;
  wire [25:0] bit_extender_2_out, controlled_buffer_4_out;
  wire [31:0] adder_1_out, adder_2_out, bit_extender_1_out;

  and u_JMP (JMP_2, ~in_2[26], in_2[27], ~in_2[28], ~in_2[29], ~in_2[30], ~in_2[31]);  // AND_Gate
  and u_BEQ (BEQ, ~in_2[27], in_2[28], ~in_2[26], ~in_2[29], ~in_2[30], ~in_2[31]);  // AND_Gate
  and u_OPALU (OPALU_2, ~in_2[26], ~in_2[27], ~in_2[28], ~in_2[29], ~in_2[30], ~in_2[31]);  // AND_Gate
  and u_HALT (HALT, in_2[26], in_2[27], in_2[28], in_2[29], in_2[30], in_2[31]);
  and ADI (ADDI, in_2[26], in_2[27], in_2[28], ~in_2[29], in_2[30], in_2[31]);  // AND_Gate
  and u_LW (LW, in_2[26], in_2[27], ~in_2[28], ~in_2[29], ~in_2[30], in_2[31]);  // AND_Gate
  and u_SW (SW, in_2[26], in_2[27], ~in_2[28], in_2[29], ~in_2[30], in_2[31]);  // AND_Gate
  Adder #(.width(32)) adder_1 (.a(PC), .b(32'h4), .out(adder_1_out));  // open: cin, cout
  assign RF2 = OPALU_2 ? in_2[20:16] : 5'bz;  // Controlled_Buffer controlled_buffer_1
  assign RF1 = LW ? in_2[25:21] : 5'bz;  // Controlled_Buffer controlled_buffer_2
  assign RF1 = SW ? in_2[25:21] : 5'bz;  // Controlled_Buffer controlled_buffer_3
  assign bit_extender_1_out = {{6{controlled_buffer_4_out[25]}}, controlled_buffer_4_out};  // Bit_Extender bit_extender_1
  assign controlled_buffer_4_out = JMP_2 ? in_2[25:0] : 26'bz;  // Controlled_Buffer controlled_buffer_4
  assign controlled_buffer_4_out = and_1_out ? bit_extender_2_out : 26'bz;  // Controlled_Buffer controlled_buffer_5
  Comparator #(.width(5)) comparator_1 (.a(in_2[25:21]), .b(in_2[20:16]), .eq(comparator_1_eq));  // open: gt, lt
  assign bit_extender_2_out = {{10{in_2[15]}}, in_2[15:0]};  // Bit_Extender bit_extender_2
  assign RF1 = OPALU_2 ? in_2[25:21] : 5'bz;  // Controlled_Buffer controlled_buffer_6
  assign OUT = ADDI ? in_2[15:0] : 16'bz;  // Controlled_Buffer controlled_buffer_7
  assign RD = ADDI ? in_2[20:16] : 5'bz;  // Controlled_Buffer controlled_buffer_8
  assign RF1 = ADDI ? in_2[25:21] : 5'bz;  // Controlled_Buffer controlled_buffer_9
  assign RD = LW ? in_2[20:16] : 5'bz;  // Controlled_Buffer controlled_buffer_10
  assign RD = SW ? in_2[20:16] : 5'bz;  // Controlled_Buffer controlled_buffer_11
  Adder #(.width(32)) adder_2 (.a(adder_1_out), .b(bit_extender_1_out), .out(adder_2_out));  // open: cin, cout
  assign JMP = JMP_2 ? adder_2_out : 32'bz;  // Controlled_Buffer controlled_buffer_12
  and and_1 (and_1_out, comparator_1_eq, BEQ);
  assign OPALU = OPALU_2 ? in_2[5:0] : 6'bz;  // Controlled_Buffer controlled_buffer_13
  assign RD = OPALU_2 ? in_2[15:11] : 5'bz;  // Controlled_Buffer controlled_buffer_14
  assign OUT = LW ? in_2[15:0] : 16'bz;  // Controlled_Buffer controlled_buffer_15
  assign OUT = SW ? in_2[15:0] : 16'bz;  // Controlled_Buffer controlled_buffer_16
  not not_1 (not_1_out, OPALU_2);
  not not_2 (not_2_out, LW);
  not not_3 (not_3_out, BEQ);
  not not_4 (not_4_out, SW);
  assign RegDst = BEQ ? not_3_out : 1'bz;  // Controlled_Buffer controlled_buffer_17
  assign RegDst = OPALU_2 ? OPALU_2 : 1'bz;  // Controlled_Buffer controlled_buffer_18
  assign RegDst = LW ? not_2_out : 1'bz;  // Controlled_Buffer controlled_buffer_19
  assign RegWrte = LW ? LW : 1'bz;  // Controlled_Buffer controlled_buffer_20
  assign RegDst = SW ? not_4_out : 1'bz;  // Controlled_Buffer controlled_buffer_21
  assign RegWrte = BEQ ? not_3_out : 1'bz;  // Controlled_Buffer controlled_buffer_22
  assign ALUSrc = BEQ ? not_3_out : 1'bz;  // Controlled_Buffer controlled_buffer_23
  assign MemWrte = BEQ ? not_3_out : 1'bz;  // Controlled_Buffer controlled_buffer_24
  assign RegWrte = OPALU_2 ? OPALU_2 : 1'bz;  // Controlled_Buffer controlled_buffer_25
  assign ALUSrc = OPALU_2 ? not_1_out : 1'bz;  // Controlled_Buffer controlled_buffer_26
  assign MemWrte = OPALU_2 ? not_1_out : 1'bz;  // Controlled_Buffer controlled_buffer_27
  assign MemRead = OPALU_2 ? not_1_out : 1'bz;  // Controlled_Buffer controlled_buffer_28
  assign ALUSrc = LW ? LW : 1'bz;  // Controlled_Buffer controlled_buffer_29
  assign MemWrte = LW ? not_2_out : 1'bz;  // Controlled_Buffer controlled_buffer_30
  assign MemRead = LW ? LW : 1'bz;  // Controlled_Buffer controlled_buffer_31
  assign RegWrte = SW ? not_4_out : 1'bz;  // Controlled_Buffer controlled_buffer_32
  assign ALUSrc = SW ? SW : 1'bz;  // Controlled_Buffer controlled_buffer_33
  assign MemWrte = SW ? SW : 1'bz;  // Controlled_Buffer controlled_buffer_34
  assign MemRead = BEQ ? not_3_out : 1'bz;  // Controlled_Buffer controlled_buffer_35
  assign MemToReg = BEQ ? not_3_out : 1'bz;  // Controlled_Buffer controlled_buffer_36
  assign MemToReg = OPALU_2 ? not_1_out : 1'bz;  // Controlled_Buffer controlled_buffer_37
  assign MemToReg = LW ? LW : 1'bz;  // Controlled_Buffer controlled_buffer_38
  assign MemRead = SW ? not_4_out : 1'bz;  // Controlled_Buffer controlled_buffer_39
  assign MemToReg = SW ? not_4_out : 1'bz;  // Controlled_Buffer controlled_buffer_40

  // Other names for the same wires on the sheet: OUTPUT[15:0] = OUT

  // Notes on the sheet:
  //   OPCODE
  //   000010
  //   111111
  //   001000
  //   100011
  //   101011
  //   dir
  //   rd
  //   rf
  //   jump dir
  //   jump
endmodule

module TTYCntrl (
  input  in_1,
  output [6:0] OUT
);

  wire [10:0] adder_1_out, counter_1_q;

  Adder #(.width(11)) adder_1 (.a(11'h1), .b(counter_1_q), .out(adder_1_out));  // open: cin, cout
  Counter #(.width(11), .max('h7ff), .ongoal("stay")) counter_1 (
    .D(adder_1_out), .Q(counter_1_q), .clk(in_1));  // open: load, count, carry, clr
  ROM #(.addrWidth(11), .dataWidth(7)) rom_1 (.addr(counter_1_q), .data(OUT));  // open: sel

  // Notes on the sheet:
  //   contents of rom_1 (hex, n*v repeats v):
  //   20 20 20 5*5f 20 5f 4*20 5f 20 5*5f 20 7*5f 5*20 5f 5f a 20 20 2f 20 4*5f 7c 20 7c 20 20 7c 20 7c 5f
  //   20 20 20 5f 7c 20 20 5f 5f 20 5c 20 5c 20 20 20 2f 20 2f a 20 7c 20 7c 4*20 7c 20 7c 5f 5f 7c 20 7c
  //   20 7c 20 7c 20 7c 20 7c 5f 5f 29 20 5c 20 5c 5f 2f 20 2f 20 a 20 7c 20 7c 4*20 7c 20 20 5f 5f 20 20
  //   7c 20 7c 20 7c 20 7c 20 20 5f 5f 5f 2f 20 5c 20 20 20 2f 20 20 a 20 7c 20 7c 4*5f 7c 20 7c 20 20 7c
  //   20 7c 5f 7c 20 7c 5f 7c 20 7c 6*20 7c 20 7c 20 20 20 a 20 20 5c 5*5f 7c 5f 7c 20 20 7c 5f 7c 5*5f 7c
  //   5f 7c 6*20 7c 5f 7c 20 20 20 a 66*20 a 4c 4f 47 49 53 49 4d 20 33 32 2d 42 49 54 20 43 50 55 9*20 4d
  //   65 6d 6f 72 69 61 73 49 54 a 56 65 72 73 69 6f 6e 20 31 2e 30 16*20 31 32 2f 30 35 2f 32 30 31 38 a
  //   a 43 50 55 20 53 70 65 63 73 a 28*2d a 41 4c 55 20 2d 20 33 32 62 69 74 73 a 52 41 4d 20 2d 20 31 6b
  //   42 a 43 4c 4f 43 4b 20 2d 20 48 7a a 52 45 47 49 53 54 45 52 53 20 2d 33 32 75 20 6f 66 20 33 32 62
  //   69 74 73 a
endmodule

// ALUCNTRL
module AluControl (
  input  alop0,
  input  alop1,
  input  [5:0] in_3,
  output [3:0] OUT
);

  wire and_1_out, and_2_out, and_3_out, and_4_out, not_1_out, not_2_out, not_3_out;

  not not_1 (not_1_out, alop1);
  not not_2 (not_2_out, alop1);
  not not_3 (not_3_out, in_3[2]);
  and and_1 (and_1_out, alop1, in_3[0]);
  and and_2 (and_2_out, alop1, in_3[3]);
  and and_3 (and_3_out, not_1_out, alop0);
  and and_4 (and_4_out, alop1, in_3[1]);
  or or_1 (OUT[1], not_2_out, not_3_out);
  or or_2 (OUT[0], and_1_out, and_2_out);
  or or_3 (OUT[2], and_3_out, and_4_out);

  assign OUT[3] = 1'b0;
endmodule
