// Logisim project fibonacci.circ as structural Verilog: 2 circuits, main circuit fib
module fib (
  input  start,
  input  [3:0] \input ,
  output [5:0] OUT,
  output halt
);

  wire clock_1_out, multiplexer_2_out;
  wire [5:0] adder_1_out, bit_extender_1_out, counter_1_q, multiplexer_1_out, register_2_q;

  Register #(.width(6)) register_1 (.D(multiplexer_1_out), .Q(OUT), .clk(multiplexer_2_out));  // open: en, clr
  Multiplexer #(.width(6), .enable("false")) multiplexer_1 (
    .in0(adder_1_out), .in1(6'b000001), .out(multiplexer_1_out), .sel(start));
  assign bit_extender_1_out = {{2{1'b0}}, \input };  // Bit_Extender bit_extender_1
  Register #(.width(6)) register_2 (.D(OUT), .Q(register_2_q), .clk(multiplexer_2_out));  // open: en, clr
  Clock clock_1 (.out(clock_1_out));
  Multiplexer #(.enable("false")) multiplexer_2 (.in0(clock_1_out), .in1(1'b0), .out(multiplexer_2_out), .sel(halt));
  Adder #(.width(6)) adder_1 (.a(register_2_q), .b(OUT), .out(adder_1_out));  // open: cin, cout
  Counter #(.width(6), .max('h3f)) counter_1 (
    .D(counter_1_q), .Q(counter_1_q), .clk(multiplexer_2_out));  // open: load, count, carry, clr
  Comparator #(.width(6)) comparator_1 (.a(counter_1_q), .b(bit_extender_1_out), .eq(halt));  // open: gt, lt
endmodule

module main (
  input  [3:0] in_1
);

  wire button_1_out, fib_1_halt;
  wire [5:0] fib_1_out;

  fib fib_1 (.\input (in_1), .start(button_1_out), .OUT(fib_1_out), .halt(fib_1_halt));
  Button button_1 (.out(button_1_out));
  LED led_1 (.in(fib_1_halt));
endmodule
